// Digital circuit atk16_alu.dig as structural Verilog
module atk16_alu (
  input  [15:0] A,
  input  [15:0] B,
  input  [2:0] S,
  output [15:0] Y,
  output [3:0] FLAGS
);

  wire MINUS_c_o, PLUS_c_o, S0, S1, S2, S3, S4, S5, S6, S7;
  wire [15:0] and_1_out, ARI_SHIFT_RIGHT_out, LOG_SHIFT_LEFT_out, LOG_SHIFT_RIGHT_out, MINUS_s, or_1_out,
       PLUS_s, xor_1_out;

  Decoder #(.Selector_Bits(3)) decoder_1 (
    .sel(S), .out_0(S0), .out_1(S1), .out_2(S2), .out_3(S3), .out_4(S4), .out_5(S5), .out_6(S6), .out_7(S7));
  Add #(.Bits(16)) PLUS (.a(A), .b(B), .c_i(1'b0), .s(PLUS_s), .c_o(PLUS_c_o));
  assign and_1_out = A & B;  // And and_1, 16 bits wide
  assign xor_1_out = A ^ B;  // XOr xor_1, 16 bits wide
  BarrelShifter #(.Bits(16), .barrelShifterMode("arithmetic"), .direction("right")) ARI_SHIFT_RIGHT (
    .in(A), .shift(B[4:0]), .out(ARI_SHIFT_RIGHT_out));
  assign {FLAGS[3], Y[14:0]} = S0 ? PLUS_s : 16'bz;  // Driver driver_1
  assign FLAGS[0] = S0 ? PLUS_c_o : 1'bz;  // Driver driver_2
  Sub #(.Bits(16)) MINUS (.a(A), .b(B), .c_i(1'b0), .s(MINUS_s), .c_o(MINUS_c_o));
  assign {FLAGS[3], Y[14:0]} = S2 ? and_1_out : 16'bz;  // Driver driver_3
  assign or_1_out = A | B;  // Or or_1, 16 bits wide
  assign {FLAGS[3], Y[14:0]} = S4 ? xor_1_out : 16'bz;  // Driver driver_4
  BarrelShifter #(.Bits(16), .direction("right")) LOG_SHIFT_RIGHT (.in(A), .shift(B[4:0]), .out(LOG_SHIFT_RIGHT_out));
  BarrelShifter #(.Bits(16)) LOG_SHIFT_LEFT (.in(A), .shift(B[4:0]), .out(LOG_SHIFT_LEFT_out));
  assign {FLAGS[3], Y[14:0]} = S6 ? ARI_SHIFT_RIGHT_out : 16'bz;  // Driver driver_5
  assign {FLAGS[3], Y[14:0]} = S1 ? MINUS_s : 16'bz;  // Driver driver_6
  assign FLAGS[0] = S1 ? MINUS_c_o : 1'bz;  // Driver driver_7
  assign {FLAGS[3], Y[14:0]} = S3 ? or_1_out : 16'bz;  // Driver driver_8
  assign {FLAGS[3], Y[14:0]} = S5 ? LOG_SHIFT_RIGHT_out : 16'bz;  // Driver driver_9
  assign {FLAGS[3], Y[14:0]} = S7 ? LOG_SHIFT_LEFT_out : 16'bz;  // Driver driver_10
  atk16_alu_fo Overflow_flag (.nA_S(S1), .A15(A[15]), .B15(B[15]), .Y15(FLAGS[3]), .FO(FLAGS[1]));
  PullDown pulldown_1 (.out(FLAGS[0]));
  atk16_alu_fz Zero_flag (.Y({FLAGS[3], Y[14:0]}), .FZ(FLAGS[2]));

  assign Y[15] = FLAGS[3];

  // Other names for the same wires on the sheet: B_L5[4:0] = B[4:0]; FC = FLAGS[0]; FO = FLAGS[1]; FZ = FLAGS[2];
  //   FS = FLAGS[3]; Y15 = FLAGS[3]

  // Notes on the sheet:
  //   A: LHS of binary ALU operation
  //   B: RHS of binary ALU operation
  //   S: ALU operation code
  //   Y: Output
  //   S   Y
  //   0   A + B
  //   1   A - B
  //   2   A and B
  //   3   A or B
  //   4   A xor B
  //   5   A >> B  # logical
  //   6   A >>> B # arithmetic
  //   7   A << B
  //   AND
  //   XOR
  //   OR
  //   Sign flag
endmodule

/* Test case PLUS test:
A      B      S FLAGS  Y
0x1    0x2    0 0b0000 0x3
0xff   0x1    0 0b0000 0x100
0x1    0xffff 0 0b0101 0x0
0x4000 0x4000 0 0b1010 0x8000
*/

/* Test case MINUS test:
A      B      S FLAGS  Y
0x10   0x1    1 0b0000 0xF
0x1    0x0    1 0b0000 0x1
0x0    0x1    1 0b1001 0xFFFF
0x8000 0x1    1 0b0010 0x7FFF
*/
