// Digital circuit atk16_alu_carryfix.dig as structural Verilog
module atk16_alu_carryfix (
  input  S2,
  input  S1,
  input  S0,
  output Y
);

  wire and_1_out, and_2_out, not_1_out, not_2_out, not_3_out;

  not not_1 (not_1_out, S2);
  not not_2 (not_2_out, S1);
  not not_3 (not_3_out, S0);
  and and_1 (and_1_out, not_1_out, not_2_out, S0);
  and and_2 (and_2_out, not_1_out, S1, not_3_out);
  or or_1 (Y, and_1_out, and_2_out);
endmodule
