// Digital circuit atk16_alu_fz.dig as structural Verilog
module atk16_alu_fz (
  input  [15:0] Y,
  output FZ
);

  wire [3:0] or_1_out;

  assign or_1_out = Y[3:0] | Y[7:4] | Y[11:8] | Y[15:12];  // Or or_1, 4 bits wide
  nor nor_1 (FZ, or_1_out[0], or_1_out[1], or_1_out[2], or_1_out[3]);
endmodule

/* Test case:
Y      FZ
0x0    1
0x1    0
0xff   0
*/
