// Digital circuit atk16_irc.dig as structural Verilog
module atk16_irc (
  input  [3:0] IRQ,
  input  [15:0] PC,
  input  MAR_IE,
  input  PC_OE,
  output [15:0] DBUS
);

  wire and_1_out, priorityencoder_1_any;
  wire [1:0] priorityencoder_1_num;
  wire [15:0] multiplexer_1_out, multiplexer_2_out;

  PriorityEncoder #(.Selector_Bits(2)) priorityencoder_1 (
    .in0(IRQ[0]), .in1(IRQ[1]), .in2(IRQ[2]), .in3(IRQ[3]), .num(priorityencoder_1_num),
    .any(priorityencoder_1_any));
  Multiplexer #(.Selector_Bits(2), .Bits(16)) multiplexer_1 (
    .sel(priorityencoder_1_num), .in_0(16'h10), .in_1(16'h11), .in_2(16'h12), .in_3(16'h13),
    .out(multiplexer_1_out));
  and and_1 (and_1_out, priorityencoder_1_any, MAR_IE);
  Multiplexer #(.Bits(16)) multiplexer_2 (
    .sel(and_1_out), .in_0(PC), .in_1(multiplexer_1_out), .out(multiplexer_2_out));
  assign DBUS = PC_OE ? multiplexer_2_out : 16'bz;  // Driver driver_1

  // Notes on the sheet:
  //   IRQ: IRQ lines
  //   PC: PC value
  //   Some IRQ active?
endmodule

/* Test case:
IRQ    PC  MAR_IE PC_OE DBUS
0b0000 0x5 0      0     Z
0b0000 0x5 0      1     0x5
0b0001 0x5 0	  1	0x5
0b0001 0x5 1	  1     0x10
0b0101 0x5 1      1     0x12
*/
