// Digital circuit atk16_jump_unit.dig as structural Verilog
// Uses OPCODE parity to choose between relative addressing mode (even parity) or absolute addressing mode (odd parity).
module atk16_jump_unit (
  input  [15:0] ADDR,
  input  [15:0] PC,
  input  IM_M,
  output [15:0] PC_RES
);

  wire not_1_out;
  wire [15:0] add_1_s;

  not not_1 (not_1_out, IM_M);
  Add #(.Bits(16)) add_1 (.a(PC), .b(ADDR), .c_i(1'b0), .s(add_1_s));  // open: c_o
  Multiplexer #(.Bits(16)) multiplexer_1 (.sel(not_1_out), .in_0(add_1_s), .in_1(ADDR), .out(PC_RES));

  // Notes on the sheet:
  //   ADDR: Jump address
  //   PC: PC value
  //   IM_M: Immediate mode on?
  //   PC_RES: Result PC value
endmodule

/* Test case:
PC    ADDR    IM_M PC_RES
10    20      0    20
10    20      1    30
*/
