// Digital circuit atk16_peripherals.dig as structural Verilog
module atk16_peripherals (
  input  IM_DS,
  input  [1:0] IT_N,
  input  OE,
  input  IE,
  input  [12:0] S,
  input  CLK,
  output [3:0] IRQ,
  output [15:0] DBUS
);

  wire and_1_out, and_2_out, and_3_out, and_4_out, and_5_out, and_6_out, comparator_1_eq, comparator_2_eq,
       decoder_1_out_0, decoder_1_out_1, decoder_1_out_2, decoder_1_out_3, IRQ0;

  Decoder #(.Selector_Bits(2)) decoder_1 (
    .sel(IT_N), .out_0(decoder_1_out_0), .out_1(decoder_1_out_1), .out_2(decoder_1_out_2),
    .out_3(decoder_1_out_3));
  Comparator #(.Bits(13)) comparator_1 (.a(S), .b(13'h1), .eq(comparator_1_eq));  // open: gt, lt
  and and_1 (and_1_out, IM_DS, decoder_1_out_0);
  and and_2 (and_2_out, IM_DS, decoder_1_out_2);
  Comparator #(.Bits(13)) comparator_2 (.a(S), .b({13{1'b0}}), .eq(comparator_2_eq));  // open: gt, lt
  and and_3 (and_3_out, comparator_1_eq, OE);
  and and_4 (and_4_out, comparator_2_eq, IE);
  RS_FF_AS rs_ff_as_1 (.S(IRQ0), .R(and_1_out), .Q(IRQ[0]));  // open: nQ
  and and_5 (and_5_out, IM_DS, decoder_1_out_1);
  RS_FF_AS rs_ff_as_2 (.S(1'b0), .R(and_2_out), .Q(IRQ[2]));  // open: nQ
  and and_6 (and_6_out, IM_DS, decoder_1_out_3);
  Terminal terminal_1 (.D(DBUS), .C(CLK), .en(and_4_out));
  Keyboard keyboard_1 (.C(CLK), .en(and_3_out), .D(DBUS), .av(IRQ0));
  RS_FF_AS rs_ff_as_3 (.S(1'b0), .R(and_5_out), .Q(IRQ[1]));  // open: nQ
  RS_FF_AS rs_ff_as_4 (.S(1'b0), .R(and_6_out), .Q(IRQ[3]));  // open: nQ
endmodule
