// Digital circuit atk16_ppu.dig as structural Verilog
module atk16_ppu (
  input  MMIO_IE,
  input  MMIO_OE,
  input  [12:0] MMIO_S,
  input  PCLK,
  input  CLK,
  input  [15:0] DBUS,
  input  [8:0] X,
  input  [7:0] Y,
  output [1:0] PR,
  output [1:0] PG,
  output [1:0] PB
);

  wire counter_1_ovf;
  wire [3:0] SCAN_BUFFER_d;

  // And and_1 has open pins: In_1=MMIO_S[11], In_2=MMIO_S[12], out=open
  RAMDualPort #(.AddrBits(7), .Bits(16)) SPRITE_MEM (
    .A({7{1'b0}}), .Din(DBUS), .str(MMIO_IE), .C(CLK), .ld(MMIO_OE));  // open: D
  Counter counter_1 (.en(1'b1), .C(PCLK), .clr(1'b0), .ovf(counter_1_ovf));  // open: out
  RAMDualPort #(.AddrBits(9), .Bits(4)) SCAN_BUFFER (
    .A(X), .Din(4'b0000), .str(1'b0), .C(counter_1_ovf), .ld(1'b1), .D(SCAN_BUFFER_d));
  // Probe SCAN BUF on SCAN_BUFFER_d
  // atk16_ppu_palette atk16_ppu_palette_1: pin names not known; wires that end beside it: SCAN_BUFFER_d[3], SCAN_BUFFER_d[2], SCAN_BUFFER_d[1], SCAN_BUFFER_d[0]

  // Notes on the sheet:
  //   MMIO_S: MMI/O selector
  //   PCLK: Pixel clock
  //   CLK: CPU clock
  //   DBUS: Data bus
  //   X: X pixel
  //   Y: Y pixel
  //   8 bits tile pattern index
  //   10 bits Y position
  //   10 bits X position
  //   1 bit H flip
  //   1 bit V flip
  //   1 bit behind background? (priority)
  //   1 bit palette select
  //   = total 4 bytes per sprite
  //   x 64 sprites
  //   = 128 words
  //   2**7 selector addresses for
  //   sprite mem, starting from 0x0800
  //   TODO
  //   TODO: 8x8x4 tile pattern memory
endmodule
