// Digital circuit atk16.dig as structural Verilog
module atk16 (
  input  clk
);

  wire ALU_OE, atk16_vga_sync_1_hsync, atk16_vga_sync_1_vsync, CLK_t, FR_IE, IM_DS, IM_EN, IM_M, IPC_IE,
       IPC_OE, IR_IE, ISRA_OE, LI_OE, MAR_IE, MEM_IE, MEM_OE, MMIO_IE, MMIO_OE, not_1_out, or_1_out, PC_CO,
       PC_IE, PC_OE, R1_OE, R2_OE, reset_1_out, RW_IE, US_RS;
  wire [1:0] atk16_ppu_1_pb, atk16_ppu_1_pg, atk16_ppu_1_pr, atk16_tpu_1_pb, atk16_tpu_1_pg, atk16_tpu_1_pr,
       GRMODE, IT_N;
  wire [2:0] atk16_decoder_1_alu_s, atk16_decoder_1_r1_s, atk16_decoder_1_r2_s, FLAG_S, US_Q;
  wire [3:0] ALU_flags, atk16_peripherals_1_irq, FR_Q, OPCODE;
  wire [5:0] multiplexer_1_out;
  wire [7:0] atk16_ucode_addr_1_addr, atk16_vga_sync_1_y;
  wire [8:0] atk16_vga_sync_1_x;
  wire [12:0] MMIO_S;
  wire [15:0] ALU_y, atk16_alu_inputs_1_a, atk16_alu_inputs_1_b, atk16_jump_unit_1_pc_res,
       atk16_regbank_1_d1, atk16_regbank_1_d2, DBUS, IPC_q, MAR_q, PC_out;
  wire [23:14] UCODE_d;

  Register #(.Bits(16)) IPC (.D(DBUS), .C(CLK_t), .en(IPC_IE), .Q(IPC_q));
  assign DBUS = IPC_OE ? IPC_q : 16'bz;  // Driver driver_1
  assign DBUS = ISRA_OE ? {14'h4, IT_N} : 16'bz;  // Driver driver_2
  Reset #(.invertOutput("false")) reset_1 (.out(reset_1_out));
  atk16_decoder atk16_decoder_1 (
    .DBUS(DBUS), .IR_IE(IR_IE), .CLK(CLK_t), .LI_OE(LI_OE), .OP(OPCODE), .RW_S(FLAG_S),
    .ALU_S(atk16_decoder_1_alu_s), .R1_S(atk16_decoder_1_r1_s), .R2_S(atk16_decoder_1_r2_s));
  or or_1 (or_1_out, US_RS, reset_1_out);
  atk16_jump_unit atk16_jump_unit_1 (.ADDR(DBUS), .PC(PC_out), .IM_M(IM_M), .PC_RES(atk16_jump_unit_1_pc_res));
  not not_1 (not_1_out, CLK_t);
  Break break_1 (.brk(or_1_out));
  Counter #(.Bits(3)) Microsequencer (.en(1'b1), .C(not_1_out), .clr(or_1_out), .out(US_Q));  // open: ovf
  atk16_peripherals atk16_peripherals_1 (
    .IM_DS(IM_DS), .IT_N(IT_N), .OE(MMIO_OE), .IE(MMIO_IE), .S(MMIO_S), .CLK(CLK_t),
    .IRQ(atk16_peripherals_1_irq), .DBUS(DBUS));
  CounterPreset #(.Bits(16), .isProgramCounter("true")) PC (
    .en(PC_CO), .C(CLK_t), .dir(1'b0), .in(atk16_jump_unit_1_pc_res), .ld(PC_IE), .clr(1'b0), .out(PC_out));  // open: ovf
  atk16_regbank atk16_regbank_1 (
    .Din(DBUS), .RW_IE(RW_IE), .RW_S(FLAG_S), .CLK(CLK_t), .R1_S(atk16_decoder_1_r1_s),
    .R2_S(atk16_decoder_1_r2_s), .D1(atk16_regbank_1_d1), .D2(atk16_regbank_1_d2));
  assign DBUS = PC_OE ? PC_out : 16'bz;  // Driver driver_3
  atk16_ucode_addr atk16_ucode_addr_1 (
    .FLAG_S(FLAG_S), .FR_Q(FR_Q), .OP(OPCODE), .US_Q(US_Q), .IRQ(atk16_peripherals_1_irq), .IM_EN(IM_EN),
    .IM_DS(IM_DS), .ADDR(atk16_ucode_addr_1_addr), .IT_N(IT_N));  // open: INT_ACTIVE
  // Probe OPCODE on OPCODE
  // Probe PC on PC_out
  // Probe Bus on DBUS
  assign DBUS = R1_OE ? atk16_regbank_1_d1 : 16'bz;  // Driver driver_4
  EEPROM #(.AddrBits(8), .Bits(24)) UCODE (
    .A(atk16_ucode_addr_1_addr), .CS(1'b1), .WE(1'b0), .OE(1'b1),
    .D({UCODE_d[23:21], IPC_OE, IPC_IE, IM_EN, IM_DS, ISRA_OE, US_RS, UCODE_d[14], FR_IE, ALU_OE, LI_OE, IM_M, IR_IE, R2_OE, R1_OE, RW_IE, MEM_OE, MEM_IE, MAR_IE, PC_OE, PC_IE, PC_CO}));
  assign DBUS = R2_OE ? atk16_regbank_1_d2 : 16'bz;  // Driver driver_5
  atk16_alu_inputs atk16_alu_inputs_1 (
    .R1(atk16_regbank_1_d1), .R2(atk16_regbank_1_d2), .R2_S(atk16_decoder_1_r2_s), .IM_M(IM_M),
    .A(atk16_alu_inputs_1_a), .B(atk16_alu_inputs_1_b));
  Register #(.Bits(16)) MAR (.D(DBUS), .C(CLK_t), .en(MAR_IE), .Q(MAR_q));
  atk16_vga_sync atk16_vga_sync_1 (
    .PCLK(clk), .HSYNC(atk16_vga_sync_1_hsync), .VSYNC(atk16_vga_sync_1_vsync), .X(atk16_vga_sync_1_x),
    .Y(atk16_vga_sync_1_y));
  atk16_alu ALU (
    .A(atk16_alu_inputs_1_a), .B(atk16_alu_inputs_1_b), .S(atk16_decoder_1_alu_s), .Y(ALU_y),
    .FLAGS(ALU_flags));
  Stop stop_1 (.stop(UCODE_d[14]));
  atk16_mem MEMORY (
    .ADDR(MAR_q), .DBUS(DBUS), .CLK(CLK_t), .MEM_IE(MEM_IE), .MEM_OE(MEM_OE), .MMIO_IE(MMIO_IE),
    .MMIO_OE(MMIO_OE), .MMIO_S(MMIO_S));
  // Probe on atk16_vga_sync_1_x
  // Probe on atk16_vga_sync_1_y
  assign DBUS = ALU_OE ? ALU_y : 16'bz;  // Driver driver_6
  Register #(.Bits(4)) FR (.D(ALU_flags), .C(CLK_t), .en(FR_IE), .Q(FR_Q));
  atk16_ppu atk16_ppu_1 (
    .MMIO_IE(MMIO_IE), .MMIO_OE(MMIO_OE), .MMIO_S(MMIO_S), .PCLK(clk), .CLK(CLK_t), .DBUS(DBUS),
    .X(atk16_vga_sync_1_x), .Y(atk16_vga_sync_1_y), .PR(atk16_ppu_1_pr), .PG(atk16_ppu_1_pg),
    .PB(atk16_ppu_1_pb));
  atk16_tpu atk16_tpu_1 (
    .MMIO_IE(MMIO_IE), .MMIO_OE(MMIO_OE), .MMIO_S(MMIO_S), .DBUS(DBUS), .X(atk16_vga_sync_1_x),
    .Y(atk16_vga_sync_1_y), .PCLK(clk), .PR(atk16_tpu_1_pr), .PG(atk16_tpu_1_pg), .PB(atk16_tpu_1_pb));
  // Probe MMIO_S on MMIO_S
  Counter #(.Bits(4)) CLK_divider__16 (.en(1'b1), .C(clk), .clr(1'b0), .ovf(CLK_t));  // open: out
  atk16_graphics_mode atk16_graphics_mode_1 (
    .DBUS(DBUS), .MMIO_S(MMIO_S), .MMIO_IE(MMIO_IE), .CLK(CLK_t), .MODE(GRMODE));
  Multiplexer #(.Selector_Bits(2), .Bits(6)) multiplexer_1 (
    .sel(GRMODE), .in_0({6{1'b0}}), .in_1({atk16_tpu_1_pb, atk16_tpu_1_pg, atk16_tpu_1_pr}),
    .in_2({atk16_ppu_1_pb, atk16_ppu_1_pg, atk16_ppu_1_pr}), .in_3({6{1'b0}}), .out(multiplexer_1_out));
  // Probe GRAPHICS MODE on GRMODE
  VGA vga_1 (
    .R(multiplexer_1_out[1:0]), .G(multiplexer_1_out[3:2]), .B(multiplexer_1_out[5:4]),
    .H(atk16_vga_sync_1_hsync), .V(atk16_vga_sync_1_vsync), .C(clk));

  // Other names for the same wires on the sheet: PCLK = clk

  // Notes on the sheet:
  //   clk: Hz: 25175000
  //   contents of UCODE (hex, n*v repeats v):
  //   c,221,3040,8000,4*0,c,221,3040,8000,4*0,c,221,3440,8000,4*0,c
  //   ,221,3440,8000,4*0,c,221,88,60,8000,0,0,0,c,221,88,60,8000,0,0,0
  //   ,c,221,88,110,8000,0,0,0,c,221,88,110,8000,0,0,0,c,221,840,8000
  //   ,4*0,c,221,840,8000,4*0,c,221,82,8000,4*0,c,221,82,8000,4*0,c
  //   ,221,c02,8000,4*0,c,221,c02,8000,4*0,c,221,8000,5*0,c,221,82,8000
  //   ,4*0,c,221,8000,5*0,c,221,c02,8000,4*0,c,221,44,8000,4*0,c,221
  //   ,44,8000,4*0,c,221,8000,5*0,c,221,8000,5*0,c,221,8000,5*0,c,221
  //   ,8000,5*0,c0004,10008,22,8000,4*0,c0004,10008,22,8000,4*0,c0004
  //   ,10008,22,8000,4*0,c0004,10008,22,8000,4*0,c,221,120002,8000,4*0
  //   ,c,221,120002,8000,4*0,c,221,4000,5*0,c,221,4000
endmodule
