// Digital circuit atk16_alu.dig as structural Verilog
module atk16_alu (
  input  [15:0] A,
  input  [15:0] B,
  input  [3:0] S,
  output [15:0] Y,
  output [3:0] FLAGS
);

  wire _74382_1_pin14, _74382_1_pin15, _74382_2_pin14, _74382_3_pin14, decoder_1_out_0, decoder_1_out_1,
       decoder_1_out_2, Y0, Y1, Y2, Y3, Y4, Y5, Y6, Y7, Y8, Y9, Y10, Y11, Y12, Y13, Y14, Y15;
  wire [1:0] or_3_out;
  wire [2:0] demultiplexer_1_out_0, demultiplexer_1_out_1;
  wire [3:0] or_2_out;
  wire [7:0] or_1_out;
  wire [15:0] demultiplexer_2_out_0, demultiplexer_2_out_1, demultiplexer_2_out_2, driver_1_out, SLL_out,
       SRA_out, SRL_out;

  Demultiplexer #(.Bits(3)) demultiplexer_1 (
    .sel(S[3]), .in(S[2:0]), .out_0(demultiplexer_1_out_0), .out_1(demultiplexer_1_out_1));
  Demultiplexer #(.Selector_Bits(3), .Bits(16)) demultiplexer_2 (
    .sel(demultiplexer_1_out_1), .in(A), .out_0(demultiplexer_2_out_0), .out_1(demultiplexer_2_out_1),
    .out_2(demultiplexer_2_out_2));  // open: out_3, out_4, out_5, out_6, out_7
  Decoder #(.Selector_Bits(3)) decoder_1 (
    .sel(demultiplexer_1_out_1), .out_0(decoder_1_out_0), .out_1(decoder_1_out_1), .out_2(decoder_1_out_2));  // open: out_3, out_4, out_5, out_6, out_7
  _74382 _74382_1 (
    .pin1(A[1]), .pin2(B[1]), .pin3(A[0]), .pin4(B[0]), .pin5(demultiplexer_1_out_0[0]),
    .pin6(demultiplexer_1_out_0[1]), .pin7(demultiplexer_1_out_0[2]), .pin8(Y0), .pin9(Y1), .pin10(1'b0),
    .pin11(Y2), .pin12(Y3), .pin14(_74382_1_pin14), .pin15(_74382_1_pin15), .pin16(B[3]), .pin17(A[3]),
    .pin18(B[2]), .pin19(A[2]), .pin20(1'b1));  // open: pin13
  atk16_alu_carryfix atk16_alu_carryfix_1 (
    .S2(demultiplexer_1_out_0[2]), .S1(demultiplexer_1_out_0[1]), .S0(demultiplexer_1_out_0[0]),
    .Y(_74382_1_pin15));
  BarrelShifter #(.Bits(16), .direction("right")) SRL (.in(demultiplexer_2_out_0), .shift(B[4:0]), .out(SRL_out));
  BarrelShifter #(.Bits(16)) SLL (.in(demultiplexer_2_out_2), .shift(B[4:0]), .out(SLL_out));
  assign driver_1_out = decoder_1_out_0 ? SRL_out : 16'bz;  // Driver driver_1
  BarrelShifter #(.Bits(16), .barrelShifterMode("arithmetic"), .direction("right")) SRA (
    .in(demultiplexer_2_out_1), .shift(B[4:0]), .out(SRA_out));
  _74382 _74382_2 (
    .pin1(A[5]), .pin2(B[5]), .pin3(A[4]), .pin4(B[4]), .pin5(demultiplexer_1_out_0[0]),
    .pin6(demultiplexer_1_out_0[1]), .pin7(demultiplexer_1_out_0[2]), .pin8(Y4), .pin9(Y5), .pin10(1'b0),
    .pin11(Y6), .pin12(Y7), .pin14(_74382_2_pin14), .pin15(_74382_1_pin14), .pin16(B[7]), .pin17(A[7]),
    .pin18(B[6]), .pin19(A[6]), .pin20(1'b1));  // open: pin13
  assign driver_1_out = decoder_1_out_2 ? SLL_out : 16'bz;  // Driver driver_2
  assign driver_1_out = decoder_1_out_1 ? SRA_out : 16'bz;  // Driver driver_3
  assign Y = S[3] ? driver_1_out : 16'bz;  // Driver driver_4
  _74382 _74382_3 (
    .pin1(A[9]), .pin2(B[9]), .pin3(A[8]), .pin4(B[8]), .pin5(demultiplexer_1_out_0[0]),
    .pin6(demultiplexer_1_out_0[1]), .pin7(demultiplexer_1_out_0[2]), .pin8(Y8), .pin9(Y9), .pin10(1'b0),
    .pin11(Y10), .pin12(Y11), .pin14(_74382_3_pin14), .pin15(_74382_2_pin14), .pin16(B[11]), .pin17(A[11]),
    .pin18(B[10]), .pin19(A[10]), .pin20(1'b1));  // open: pin13
  assign Y = ~S[3] ? {Y15, Y14, Y13, Y12, Y11, Y10, Y9, Y8, Y7, Y6, Y5, Y4, Y3, Y2, Y1, Y0} : 16'bz;  // DriverInvSel driverinvsel_1
  _74382 _74382_4 (
    .pin1(A[13]), .pin2(B[13]), .pin3(A[12]), .pin4(B[12]), .pin5(demultiplexer_1_out_0[0]),
    .pin6(demultiplexer_1_out_0[1]), .pin7(demultiplexer_1_out_0[2]), .pin8(Y12), .pin9(Y13), .pin10(1'b0),
    .pin11(Y14), .pin12(Y15), .pin13(FLAGS[1]), .pin14(FLAGS[0]), .pin15(_74382_3_pin14), .pin16(B[15]),
    .pin17(A[15]), .pin18(B[14]), .pin19(A[14]), .pin20(1'b1));
  assign or_1_out = Y[7:0] | Y[15:8];  // Or or_1, 8 bits wide
  BitSelector #(.Selector_Bits(4)) bitselector_1 (.in(Y), .sel(4'b1111), .out(FLAGS[3]));
  assign or_2_out = or_1_out[3:0] | or_1_out[7:4];  // Or or_2, 4 bits wide
  assign or_3_out = or_2_out[1:0] | or_2_out[3:2];  // Or or_3, 2 bits wide
  nor nor_1 (FLAGS[2], or_3_out[0], or_3_out[1]);

  // Other names for the same wires on the sheet: ALS_E = S[3]

  // Notes on the sheet:
  //   A: LHS of binary ALU operation
  //   B: RHS of binary ALU operation
  //   S: ALU operation code
  //   Y: ALU output
endmodule

/* Test case Add test 1:
A B S FLAGS Y
0x1 0x2 3 0b0000 0x3
0xff 0x1 3 0b0000 0x100
0x1 0xffff 3 0b0101 0x0
*/

/* Test case Sub test 1:
A B S FLAGS Y
0x10 0x1 2 0b0001 0xF
0x1 0x0 1 0b1000 0xFFFF
*/
