// Digital circuit atk16_alu_inputs.dig as structural Verilog
// Maps the R1 input to the A output. Uses OPCODE parity to mux either the R2 input (even parity) or the RW_S input, here acting as a small immediate value, to the B output.
module atk16_alu_inputs (
  input  [15:0] R1,
  input  [15:0] R2,
  input  [2:0] R2_S,
  input  [3:0] OPCODE,
  output [15:0] A,
  output [15:0] B
);

  Multiplexer #(.Bits(16)) multiplexer_1 (.sel(OPCODE[0]), .in_0(R2), .in_1({{13{1'b0}}, R2_S}), .out(B));

  assign A = R1;

  // Notes on the sheet:
  //   R1: Register 1 value from regbank
  //   R2: Register 2 value from regbank
  //   R2_S: Register 2 selector
  //   OPCODE: Opcode
  //   A: Output A
  //   B: Output B
endmodule
