// Digital circuit atk16_decoder.dig as structural Verilog
module atk16_decoder (
  input  [15:0] DBUS,
  input  IR_IE,
  input  CLK,
  input  LI_OE,
  output [3:0] OP,
  output [2:0] RW_S,
  output [2:0] ALU_S,
  output [2:0] R1_S,
  output [2:0] R2_S
);

  wire [15:0] bitextender_1_out;

  Register #(.Bits(16)) IR (.D(DBUS), .C(CLK), .en(IR_IE), .Q({OP, RW_S, R1_S, R2_S, ALU_S}));
  BitExtender #(.inputBits(9)) bitextender_1 (.in({R1_S, R2_S, ALU_S}), .out(bitextender_1_out));
  assign DBUS = LI_OE ? bitextender_1_out : 16'bz;  // Driver driver_1

  // Notes on the sheet:
  //   IR_IE: Instruction register input enable
  //   OP: Opcode
  //   RW_S: Write register selection
  //   ALU_S: ALU selection code
  //   R1_S: Read register 1 selection
  //   R2_S: Read register 2 selection
  //   LI_OE: Low 9 bits immediate value output enable
endmodule

/* Test case:
CLK DBUS               IR_IE LI_OE OP RW_S R1_S R2_S ALU_S
C   0b0000001010011000 1     0     0  1    2    3    0
*/
