// Digital circuit atk16_graphics_mode.dig as structural Verilog
module atk16_graphics_mode (
  input  [15:0] DBUS,
  input  [12:0] MMIO_S,
  input  MMIO_IE,
  input  CLK,
  output [1:0] MODE
);

  wire and_1_out, and_2_out;
  wire [12:0] xnor_1_out;

  assign xnor_1_out = ~(MMIO_S ^ 13'h2);  // XNOr xnor_1, 13 bits wide
  and and_1 (and_1_out, xnor_1_out[0], xnor_1_out[1], xnor_1_out[2], xnor_1_out[3], xnor_1_out[4], xnor_1_out[5], xnor_1_out[6], xnor_1_out[7], xnor_1_out[8], xnor_1_out[9], xnor_1_out[10], xnor_1_out[11], xnor_1_out[12]);
  Register #(.Bits(2)) GRAPHICS_MODE (.D(DBUS[1:0]), .C(CLK), .en(and_2_out), .Q(MODE));
  and and_2 (and_2_out, and_1_out, MMIO_IE);

  // Notes on the sheet:
  //   MODE: 00 disabled
  //   01 text mode
  //   10 sprite mode
  //   11 undefined
endmodule
