// Digital circuit atk16_jump_unit.dig as structural Verilog
// Uses OPCODE parity to choose between relative addressing mode (even parity) or absolute addressing mode (odd parity).
module atk16_jump_unit (
  input  [15:0] ADDR,
  input  [15:0] PC,
  input  [3:0] OPCODE,
  output [15:0] PC_RES
);

  wire [15:0] add_1_s;

  Add #(.Bits(16)) add_1 (.a(PC), .b(ADDR), .c_i(1'b0), .s(add_1_s));  // open: c_o
  Multiplexer #(.Bits(16)) multiplexer_1 (.sel(OPCODE[0]), .in_0(add_1_s), .in_1(ADDR), .out(PC_RES));

  // Notes on the sheet:
  //   ADDR: Jump address
  //   PC: PC value
  //   OPCODE: OPCODE
  //   PC_RES: Result PC value
  //   OP parity bit
endmodule

/* Test case:
PC    ADDR    OPCODE    PC_RES
10    20      0b0101    20
10    20      0b0110    30
*/
