// Digital circuit atk16_mem.dig as structural Verilog
module atk16_mem (
  input  [15:0] ADDR,
  input  [15:0] DBUS,
  input  CLK,
  input  MEM_IE,
  input  MEM_OE,
  output MMIO_IE,
  output MMIO_OE,
  output [12:0] MMIO_S
);

  wire and_3_out, and_4_out, MMIO_IE_t, MMIO_OE_t, RAM_IE, RAM_OE, ROM_OE;
  wire [1:0] atk16_mem_mux_1_x;
  wire [14:0] demultiplexer_1_out_0, demultiplexer_1_out_1;
  wire [15:0] MEM_RAM_d, MEM_ROM_d;

  atk16_mem_mux atk16_mem_mux_1 (
    .C(ADDR[13]), .B(ADDR[14]), .A(ADDR[15]), .X(atk16_mem_mux_1_x[0]), .Y(atk16_mem_mux_1_x[1]));
  Demultiplexer #(.Selector_Bits(2), .Bits(15)) demultiplexer_1 (
    .sel(atk16_mem_mux_1_x), .in(ADDR[14:0]), .out_0(demultiplexer_1_out_0), .out_1(demultiplexer_1_out_1));  // open: out_2, out_3
  Decoder #(.Selector_Bits(2)) decoder_1 (
    .sel(atk16_mem_mux_1_x), .out_0(ROM_OE), .out_1(RAM_OE), .out_2(MMIO_OE_t));  // open: out_3
  Demultiplexer #(.Selector_Bits(2)) demultiplexer_2 (
    .sel(atk16_mem_mux_1_x), .in(MEM_IE), .out_1(RAM_IE), .out_2(MMIO_IE_t));  // open: out_0, out_3
  RAMDualPort #(.AddrBits(15), .Bits(16)) MEM_RAM (
    .A(demultiplexer_1_out_1), .Din(DBUS), .str(RAM_IE), .C(CLK), .ld(1'b1), .D(MEM_RAM_d));
  EEPROM #(.AddrBits(15), .isProgramMemory("true"), .Bits(16)) MEM_ROM (
    .A(demultiplexer_1_out_0), .CS(1'b1), .WE(1'b0), .OE(1'b1), .D(MEM_ROM_d));
  // Probe RAM_OUT on MEM_RAM_d
  and and_1 (MMIO_IE, MMIO_IE_t, MEM_IE);
  and and_2 (MMIO_OE, MMIO_OE_t, MEM_OE);
  // Probe ROM_OUT on MEM_ROM_d
  assign DBUS = and_4_out ? MEM_RAM_d : 16'bz;  // Driver driver_1
  assign DBUS = and_3_out ? MEM_ROM_d : 16'bz;  // Driver driver_2
  and and_3 (and_3_out, ROM_OE, MEM_OE);
  and and_4 (and_4_out, RAM_OE, MEM_OE);

  assign MMIO_S = ADDR[12:0];

  // Notes on the sheet:
  //   ADDR: Address
  //   DBUS: Data bus
  //   CLK: Clock
  //   MMIO_IE: Memory-mapped I/O word input enable
  //   MMIO_OE: Memory-mapped I/O word output enable
  //   MEM_IE: Memory input enable
  //   MEM_OE: Memory output enable
  //   MMIO_S: Memory-mapped I/O word selector
  //   contents of MEM_ROM (hex, n*v repeats v):
  //   4014,2e00,1dc0,6027,8000,8000,8000,8000,8000,8000,8000,8000,8000,8000,8000,8000,001c,001a,001a,
  //   001a,8000,e000,e001,e002,e800,f800,4855,f000,31c0,1fc8,31c8,1fc8,4016,2000,2000,4215,2240,3040,
  //   1fc9,23c0,1fc9,21c0,e000,4017,2000,4200,3008,6018,0001,0017,0019,0041,001a,4433,2480,31d0,1fc8,
  //   4400,0590,2480,31d0,1fc8,1fc9,27c0,1fc9,25c0,0498,31d0,1fc8,1d89,2380,5040,1fd8,4431,2480,31d0,
  //   1fc8,1fc9,25c0,2480,31d0,1fc8,1fc9,21c0,4200,0270,3040,4432,2480,31d0,1fc8,1fc9,25c0,2480,31d0,
  //   1fc8,1fc9,21c0,4201,0270,3040,4000,0180,2000,31c0,1fc8,4030,2000,31c0,1fc8,1fc9,23c0,1fc9,21c0,
  //   3008,4000,31c0,1fc8,1fc9,21c0,4400,31d0,1fc8,1fc9,21c0,4202,0270,3040,4202,0388,2240,31c8,1fc8,
  //   4234,2240,31c8,1fc8,1fc9,25c0,1fc9,23c0,0251,8004,4200,31c8,1fc8,6003,4201,31c8,1fc8,1fc9,21c0,
  //   1000,8447,4001,0180,2000,31c0,1fc8,4002,0180,2000,31c0,1fc8,1fc9,23c0,1fc9,21c0,0008,31c0,1fc8,
  //   31f0,1fc8,4000,31c0,1fc8,4002,0180,2000,31c0,1fc8,1dd1,9000,1020,3180,1d88,617a,1fc9,21c0,1f80,
  //   1fc9,2dc0,31c0,1fc8,1fc9,23c0,1fc9,21c0,3008,4000,31c0,1fc8,1fc9,21c0,4402,0590,2480,31d0,1fc8,
  //   4401,31d0,1fc8,1fc9,27c0,1fc9,25c0,0498,31d0,1fc8,1fc9,21c0,4202,0270,3040,619f,4201,31c8,1fc8,
  //   1fc9,21c0,1000,8401,61f8,1f80,f000
endmodule

/* Test case:
CLK ADDR   MEM_IE  MEM_OE   DBUS  DBUS_out

# read ROM
program(0xFF)
C   0x0    0       1        Z      0xFF

# read RAM
memory MEM_RAM(0x0)=0x55;
C   0      0       0        Z      X
C   0x8000 0       1        Z      0x55

# write to RAM
C   0x8000 1       0        0xAA   0xAA
C   0x8000 0       1        Z      0xAA
*/
