// Digital circuit atk16_mem_mux.dig as structural Verilog
module atk16_mem_mux (
  input  C,
  input  B,
  input  A,
  output X,
  output Y
);

  wire and_2_out, and_3_out, not_1_out, not_2_out;

  not not_1 (not_1_out, B);
  not not_2 (not_2_out, C);
  and and_1 (Y, A, B, C);
  and and_2 (and_2_out, A, not_1_out);
  and and_3 (and_3_out, A, not_2_out);
  or or_1 (X, and_2_out, and_3_out);
endmodule
