// Digital circuit atk16_ppu.dig as structural Verilog
module atk16_ppu (
  input  PCLK,
  input  CLK,
  input  MMIO_IE,
  input  MMIO_OE,
  input  [15:0] DBUS,
  input  [12:0] MMIO_S,
  output [1:0] PR,
  output [1:0] PG,
  output [1:0] PB,
  output HSYNC,
  output [1:0] VSYNC
);

  wire comparator_1_gt, comparator_2_gt, comparator_3_gt, comparator_4_lt, comparator_5_gt, comparator_6_lt,
       counter_1_ovf;
  wire [0:0] sub_1_s, sub_2_s;
  wire [3:0] SCAN_BUFFER_d;
  wire [8:0] X, Y;
  wire [9:0] counter_2_out, counter_3_out;

  // And and_1 has open pins: In_1=MMIO_S[11], In_2=MMIO_S[12], out=open
  RAMDualPort #(.AddrBits(7), .Bits(16)) SPRITE_MEM (
    .A({7{1'b0}}), .Din(DBUS), .str(MMIO_IE), .C(CLK), .ld(MMIO_OE));  // open: D
  Counter counter_1 (.en(1'b1), .C(PCLK), .clr(1'b0), .ovf(counter_1_ovf));  // open: out
  RAMDualPort #(.AddrBits(9), .Bits(4)) SCAN_BUFFER (
    .A(X), .Din(4'b0000), .str(1'b0), .C(counter_1_ovf), .ld(1'b1), .D(SCAN_BUFFER_d));
  // Probe SCAN BUF on SCAN_BUFFER_d
  Counter #(.Bits(10)) counter_2 (.en(1'b1), .C(PCLK), .clr(comparator_1_gt), .out(counter_2_out));  // open: ovf
  Counter #(.Bits(10)) counter_3 (
    .en(1'b1), .C(comparator_1_gt), .clr(comparator_2_gt), .out(counter_3_out));  // open: ovf
  // atk16_ppu_palette atk16_ppu_palette_1: pin names not known; wires that end beside it: SCAN_BUFFER_d[3], SCAN_BUFFER_d[2], SCAN_BUFFER_d[1], SCAN_BUFFER_d[0]
  Comparator #(.Bits(10)) comparator_1 (.a(counter_2_out), .b(10'h31e), .gt(comparator_1_gt));  // open: eq, lt
  Comparator #(.Bits(10)) comparator_2 (.a(counter_3_out), .b(10'h20b), .gt(comparator_2_gt));  // open: eq, lt
  Comparator #(.Bits(10)) comparator_3 (.a(counter_2_out), .b(10'h10), .gt(comparator_3_gt));  // open: eq, lt
  Comparator #(.Bits(10)) comparator_4 (.a(counter_2_out), .b(10'h71), .lt(comparator_4_lt));  // open: gt, eq
  Sub #(.Bits(10)) sub_1 (.a(counter_2_out), .b(10'ha0), .c_i(1'b0), .s({X, sub_1_s[0]}));  // open: c_o
  Comparator #(.Bits(10)) comparator_5 (.a(counter_3_out), .b(10'ha), .gt(comparator_5_gt));  // open: eq, lt
  Comparator #(.Bits(10)) comparator_6 (.a(counter_3_out), .b(10'hd), .lt(comparator_6_lt));  // open: gt, eq
  Sub #(.Bits(10)) sub_2 (.a(counter_3_out), .b(10'h2d), .c_i(1'b0), .s({Y, sub_2_s[0]}));  // open: c_o
  nand nand_1 (HSYNC, comparator_3_gt, comparator_4_lt);
  nand nand_2 (VSYNC[0], comparator_5_gt, comparator_6_lt);
  // Pins of 1 and 2 bits meet at VSYNC

  // Notes on the sheet:
  //   PCLK: Pixel clock
  //   CLK: CPU clock
  //   DBUS: Data bus
  //   MMIO_S: MMI/O selector
  //   8 bits tile pattern index
  //   10 bits Y position
  //   10 bits X position
  //   1 bit H flip
  //   1 bit V flip
  //   1 bit behind background? (priority)
  //   1 bit palette select
  //   = total 4 bytes per sprite
  //   x 64 sprites
  //   = 128 words
  //   2**7 selector addresses for
  //   sprite mem, starting from 0x0800
  //   TODO
  //   TODO: 8x8x4 tile pattern memory
  //   Div 2
endmodule
