// Digital circuit atk16_tpu.dig as structural Verilog
module atk16_tpu (
  input  MMIO_IE,
  input  MMIO_OE,
  input  [12:0] MMIO_S,
  input  [15:0] DBUS,
  input  [8:0] X,
  input  [7:0] Y,
  input  PCLK,
  output [1:0] PR,
  output [1:0] PG,
  output [1:0] PB
);

  wire CLK, MMIOMATCH;
  wire [7:0] CHAR_S, CHARMEM_d;
  wire [10:0] multiplexer_1_out;

  and and_1 (MMIOMATCH, MMIO_S[11], MMIO_S[12], MMIO_IE);
  Counter CLK_divider__4 (.en(1'b1), .C(PCLK), .clr(1'b0), .ovf(CLK));  // open: out
  Multiplexer #(.Bits(11)) multiplexer_1 (
    .sel(MMIOMATCH), .in_0({Y[7:3], X[8:3]}), .in_1(MMIO_S[10:0]), .out(multiplexer_1_out));
  RAMDualPort #(.AddrBits(11), .Bits(8)) TEXTMEM (
    .A(multiplexer_1_out), .Din(DBUS[7:0]), .str(MMIOMATCH), .C(CLK), .ld(1'b1), .D(CHAR_S));
  // Probe on CHAR_S
  EEPROM #(.AddrBits(11), .Bits(8)) CHARMEM (.A({CHAR_S, Y[2:0]}), .CS(1'b1), .WE(1'b0), .OE(1'b1), .D(CHARMEM_d));
  // Probe on CHARMEM_d
  BitSelector #(.Selector_Bits(3)) bitselector_1 (.in(CHARMEM_d), .sel(X[2:0]), .out(PB[1]));
  // Probe on X[2:0]
  // Probe on PB[1]

  assign PB[0] = PB[1];
  assign PG = {2{PB[1]}};
  assign PR = {2{PB[1]}};

  // Other names for the same wires on the sheet: CCOLOR = PB[1]; DBUS_L8[7:0] = DBUS[7:0];
  //   MMIOADDR[10:0] = MMIO_S[10:0]; CX[2:0] = X[2:0]; TX[5:0] = X[8:3]; CY[2:0] = Y[2:0]; TY[4:0] = Y[7:3]

  // Notes on the sheet:
  //   MMIO_S: MMI/O selector
  //   DBUS: Data bus
  //   X: X pixel
  //   Y: Y pixel
  //   PCLK: Pixel clock
  //   contents of CHARMEM (hex, n*v repeats v):
  //   8*0,7e,81,a5,81,bd,99,81,7e,7e,ff,db,ff,c3,e7,ff,7e,36,7f,7f,7f
  //   ,3e,1c,8,0,8,1c,3e,7f,3e,1c,8,0,1c,3e,1c,7f,7f,6b,8,1c,8,8,1c
  //   ,3e,7f,3e,8,1c,0,0,18,3c,3c,18,0,0,ff,ff,e7,c3,c3,e7,ff,ff,0,3c
  //   ,66,42,42,66,3c,9*0,f0,e0,f0,be,33,33,33,1e,3c,66,66,66,3c,18
  //   ,7e,18,fc,cc,fc,c,c,e,f,7,fe,c6,fe,c6,c6,e6,67,3,18,db,3c,e7,e7
  //   ,3c,db,18,1,7,1f,7f,1f,7,1,0,40,70,7c,7f,7c,70,40,0,18,3c,7e,18,18
  //   ,7e,3c,18,5*66,0,66,0,fe,db,db,de,d8,d8,d8,0,7c,c6,1c,36,36,1c
  //   ,33,1e,4*0,7e,7e,7e,0,18,3c,7e,18,7e,3c,18,ff,18,3c,7e,4*18,0
  //   ,4*18,7e,3c,18,0,0,18,30,7f,30,18,0,0,0,c,6,7f,6,c,4*0,3,3,3,7f
  //   ,0,0,0,24,66,ff,66,24,0,0,0,18,3c,7e,ff,ff,0,0,0,ff,ff,7e,3c,18
  //   ,10*0,c,1e,1e,c,c,0,c,0,36,36,36,5*0,36,36,7f,36,7f,36,36,0,c
  //   ,3e,3,1e,30,1f,c,0,0,63,33,18,c,66,63,0,1c,36,1c,6e,3b,33,6e,0
  //   ,6,6,3,5*0,18,c,6,6,6,c,18,0,6,c,18,18,18,c,6,0,0,66,3c,ff,3c
  //   ,66,0,0,0,c,c,3f,c,c,7*0,c,c,6,0,0,0,3f,9*0,c,c,0,60,30,18,c,6
  //   ,3,1,0,3e,63,73,7b,6f,67,3e,0,c,e,4*c,3f,0,1e,33,30,1c,6,33,3f
  //   ,0,1e,33,30,1c,30,33,1e,0,38,3c,36,33,7f,30,78,0,3f,3,1f,30,30
  //   ,33,1e,0,1c,6,3,1f,33,33,1e,0,3f,33,30,18,c,c,c,0,1e,33,33,1e
  //   ,33,33,1e,0,1e,33,33,3e,30,18,e,0,0,c,c,0,0,c,c,0,0,c,c,0,0,c,c
  //   ,6,18,c,6,3,6,c,18,0,0,0,3f,0,0,3f,0,0,6,c,18,30,18,c,6,0,1e,33
  //   ,30,18,c,0,c,0,3e,63,7b,7b,7b,3,1e,0,c,1e,33,33,3f,33,33,0,3f
  //   ,66,66,3e,66,66,3f,0,3c,66,3,3,3,66,3c,0,1f,36,66,66,66,36,1f
  //   ,0,7f,46,16,1e,16,46,7f,0,7f,46,16,1e,16,6,f,0,3c,66,3,3,73,66
  //   ,7c,0,33,33,33,3f,33,33,33,0,1e,5*c,1e,0,78,30,30,30,33,33,1e
  //   ,0,67,66,36,1e,36,66,67,0,f,6,6,6,46,66,7f,0,63,77,7f,7f,6b,63,63
  //   ,0,63,67,6f,7b,73,63,63,0,1c,36,63,63,63,36,1c,0,3f,66,66,3e,6,6
  //   ,f,0,1e,33,33,33,3b,1e,38,0,3f,66,66,3e,36,66,67,0,1e,33,6,c,18
  //   ,33,1e,0,3f,2d,4*c,1e,0,6*33,3f,0,5*33,1e,c,0,63,63,63,6b,7f,77
  //   ,63,0,63,63,36,1c,1c,36,63,0,33,33,33,1e,c,c,1e,0,7f,63,31,18
  //   ,4c,66,7f,0,1e,5*6,1e,0,3,6,c,18,30,60,40,0,1e,5*18,1e,0,8,1c
  //   ,36,63,11*0,ff,c,c,18,7*0,1e,30,3e,33,6e,0,7,6,6,3e,66,66,3b,0,0,0
  //   ,1e,33,3,33,1e,0,38,30,30,3e,33,33,6e,0,0,0,1e,33,3f,3,1e,0,1c
  //   ,36,6,f,6,6,f,0,0,0,6e,33,33,3e,30,1f,7,6,36,6e,66,66,67,0,c,0
  //   ,e,c,c,c,1e,0,30,0,30,30,30,33,33,1e,7,6,66,36,1e,36,67,0,e,5*c
  //   ,1e,0,0,0,33,7f,7f,6b,63,0,0,0,1f,4*33,0,0,0,1e,33,33,33,1e,0,0,0
  //   ,3b,66,66,3e,6,f,0,0,6e,33,33,3e,30,78,0,0,3b,6e,66,6,f,0,0,0
  //   ,3e,3,1e,30,1f,0,8,c,3e,c,c,2c,18,0,0,0,4*33,6e,0,0,0,33,33,33
  //   ,1e,c,0,0,0,63,6b,7f,7f,36,0,0,0,63,36,1c,36,63,0,0,0,33,33,33
  //   ,3e,30,1f,0,0,3f,19,c,26,3f,0,38,c,c,7,c,c,38,0,18,18,18,0,18,18,18
  //   ,0,7,c,c,38,c,c,7,0,6e,3b,7*0,8,1c,36,63,63,7f,0,0,fe,4*82,fe
  //   ,0,0,fe,4*82,fe,0,0,fe,4*82,fe,0,0,fe,4*82,fe,0,0,fe,4*82,fe,0,0
  //   ,fe,4*82,fe,0,0,fe,4*82,fe,0,0,fe,4*82,fe,0,0,fe,4*82,fe,0,0,fe
  //   ,4*82,fe,0,0,fe,4*82,fe,0,0,fe,4*82,fe,0,0,fe,4*82,fe,0,0,fe,4*82
  //   ,fe,0,0,fe,4*82,fe,0,0,fe,4*82,fe,0,0,fe,4*82,fe,0,0,fe,4*82,fe
  //   ,0,0,fe,4*82,fe,0,0,fe,4*82,fe,0,0,fe,4*82,fe,0,0,fe,4*82,fe,0,0
  //   ,fe,4*82,fe,0,0,fe,4*82,fe,0,0,fe,4*82,fe,0,0,fe,4*82,fe,0,0,fe
  //   ,4*82,fe,0,0,fe,4*82,fe,0,0,fe,4*82,fe,0,0,fe,4*82,fe,0,0,fe,4*82
  //   ,fe,0,0,fe,4*82,fe,9*0,18,18,0,4*18,0,18,18,7e,3,3,7e,18,18,1c
  //   ,36,26,f,6,67,3f,0,0,fe,4*82,fe,0,33,33,1e,3f,c,3f,c,c,0,fe,4*82
  //   ,fe,0,7c,c6,1c,36,36,1c,33,1e,0,fe,4*82,fe,0,0,fe,4*82,fe,0,3c
  //   ,36,36,7c,0,7e,0,0,0,cc,66,33,66,cc,5*0,3f,30,30,0,0,0,fe,4*82
  //   ,fe,0,0,fe,4*82,fe,0,0,fe,4*82,fe,0,1c,36,36,1c,4*0,c,c,3f,c,c
  //   ,0,3f,0,e,18,c,6,1e,4*0,fe,4*82,fe,0,0,fe,4*82,fe,0,0,4*66,3e
  //   ,6,3,fe,db,db,de,d8,d8,d8,5*0,18,4*0,fe,4*82,fe,0,0,fe,4*82,fe
  //   ,0,1c,36,36,1c,0,3e,0,0,0,33,66,cc,66,33,0,0,c3,63,33,db,ec,f6
  //   ,f3,c0,c3,63,33,7b,cc,66,33,f0,0,fe,4*82,fe,0,c,0,c,6,3,33,1e
  //   ,0,0,fe,4*82,fe,0,0,fe,4*82,fe,0,0,fe,4*82,fe,0,0,fe,4*82,fe,0
  //   ,63,1c,36,63,7f,63,63,0,c,c,0,1e,33,3f,33,0,7c,36,33,7f,33,33
  //   ,73,0,1e,33,3,33,1e,18,30,1e,0,fe,4*82,fe,0,38,0,3f,6,1e,6,3f
  //   ,0,0,fe,4*82,fe,0,0,fe,4*82,fe,0,0,fe,4*82,fe,0,0,fe,4*82,fe,0,0
  //   ,fe,4*82,fe,0,0,fe,4*82,fe,0,0,fe,4*82,fe,0,3f,0,33,37,3f,3b,33
  //   ,0,0,fe,4*82,fe,0,0,fe,4*82,fe,0,0,fe,4*82,fe,0,0,fe,4*82,fe,0
  //   ,c3,18,3c,66,66,3c,18,0,0,fe,4*82,fe,0,0,fe,4*82,fe,0,0,fe,4*82
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endmodule
