// Digital circuit atk16_ucode_addr.dig as structural Verilog
module atk16_ucode_addr (
  input  [2:0] FLAG_S,
  input  [3:0] FR_Q,
  input  [3:0] OP,
  input  [2:0] US_Q,
  input  [3:0] IRQ,
  input  IM_EN,
  input  IM_DS,
  output [7:0] ADDR,
  output [1:0] IT_N,
  output INT_ACTIVE
);

  wire and_1_out, comparator_1_eq, FC, INT_MASK_nq, Interrupts_any;
  wire [1:0] Interrupts_num;

  PriorityEncoder #(.Selector_Bits(2)) Interrupts (
    .in0(IRQ[0]), .in1(IRQ[1]), .in2(IRQ[2]), .in3(IRQ[3]), .num(Interrupts_num), .any(Interrupts_any));
  BitSelector #(.Selector_Bits(2)) bitselector_1 (.in(FR_Q), .sel(FLAG_S[1:0]), .out(FC));
  Register #(.Bits(2)) INT_LINE (.D(Interrupts_num), .C(comparator_1_eq), .en(1'b1), .Q(IT_N));
  RS_FF_AS INT_MASK (.S(IM_EN), .R(IM_DS), .nQ(INT_MASK_nq));  // open: Q
  Comparator #(.Bits(3)) comparator_1 (.a(US_Q), .b(3'b000), .eq(comparator_1_eq));  // open: gt, lt
  and and_1 (and_1_out, Interrupts_any, INT_MASK_nq);
  Multiplexer #(.Bits(5)) multiplexer_1 (.sel(INT_ACTIVE), .in_0({OP, FC}), .in_1({3'b110, IT_N}), .out(ADDR[7:3]));
  D_FF d_ff_1 (.D(and_1_out), .C(comparator_1_eq), .Q(INT_ACTIVE));  // open: nQ

  assign ADDR[2:0] = US_Q;

  // Notes on the sheet:
  //   FLAG_S: Flag selector from instruction
  //   FR_Q: Flag register output value
  //   OP: OPCODE
  //   US_Q: Microsequencer value
  //   IRQ: Interrupt request bus
  //   IT_N: Interrupt number
  //   IM_EN: Interrupt mask assert active
  //   IM_DS: Interrupt mask assert not active
endmodule
