// Digital circuit atk16_vga_sync.dig as structural Verilog
module atk16_vga_sync (
  input  PCLK,
  output HSYNC,
  output VSYNC,
  output [8:0] X,
  output [7:0] Y
);

  wire comparator_1_gt, comparator_2_gt, comparator_3_gt, comparator_4_lt, comparator_5_gt, comparator_6_lt,
       comparator_7_gt, comparator_8_gt;
  wire [9:0] counter_1_out, counter_2_out, sub_1_s, sub_2_s;

  Counter #(.Bits(10)) counter_1 (.en(1'b1), .C(PCLK), .clr(comparator_1_gt), .out(counter_1_out));  // open: ovf
  Counter #(.Bits(10)) counter_2 (
    .en(1'b1), .C(comparator_1_gt), .clr(comparator_2_gt), .out(counter_2_out));  // open: ovf
  // Probe on counter_1_out
  Comparator #(.Bits(10)) comparator_1 (.a(counter_1_out), .b(10'h31e), .gt(comparator_1_gt));  // open: eq, lt
  Comparator #(.Bits(10)) comparator_2 (.a(counter_2_out), .b(10'h20b), .gt(comparator_2_gt));  // open: eq, lt
  Comparator #(.Bits(10)) comparator_3 (.a(counter_1_out), .b(10'h10), .gt(comparator_3_gt));  // open: eq, lt
  Comparator #(.Bits(10)) comparator_4 (.a(counter_1_out), .b(10'h71), .lt(comparator_4_lt));  // open: gt, eq
  Sub #(.Bits(10)) sub_1 (.a(counter_1_out), .b(10'ha0), .c_i(1'b0), .s(sub_1_s));  // open: c_o
  Comparator #(.Bits(10)) comparator_5 (.a(counter_2_out), .b(10'ha), .gt(comparator_5_gt));  // open: eq, lt
  Comparator #(.Bits(10)) comparator_6 (.a(counter_2_out), .b(10'hd), .lt(comparator_6_lt));  // open: gt, eq
  Sub #(.Bits(10)) sub_2 (.a(counter_2_out), .b(10'h2d), .c_i(1'b0), .s(sub_2_s));  // open: c_o
  nand nand_1 (HSYNC, comparator_3_gt, comparator_4_lt);
  // Probe on sub_1_s
  nand nand_2 (VSYNC, comparator_5_gt, comparator_6_lt);
  Comparator #(.Bits(9)) comparator_7 (.a(sub_1_s[9:1]), .b(9'h13f), .gt(comparator_7_gt));  // open: eq, lt
  Comparator #(.Bits(8)) comparator_8 (.a(sub_2_s[8:1]), .b(8'hef), .gt(comparator_8_gt));  // open: eq, lt
  Multiplexer #(.Bits(9)) multiplexer_1 (.sel(comparator_7_gt), .in_0(sub_1_s[9:1]), .in_1({9{1'b1}}), .out(X));
  Multiplexer #(.Bits(8)) multiplexer_2 (.sel(comparator_8_gt), .in_0(sub_2_s[8:1]), .in_1({8{1'b1}}), .out(Y));

  // Notes on the sheet:
  //   Div 2
endmodule
