// Digital circuit atk16_alu_fo.dig as structural Verilog
module atk16_alu_fo (
  input  nA_S,
  input  A15,
  input  B15,
  input  Y15,
  output FO
);

  wire and_1_out, and_2_out, and_3_out, and_4_out, not_1_out, not_2_out, not_3_out, not_4_out;

  not not_1 (not_1_out, nA_S);
  not not_2 (not_2_out, A15);
  not not_3 (not_3_out, B15);
  not not_4 (not_4_out, Y15);
  and and_1 (and_1_out, not_2_out, not_3_out, Y15, not_1_out);
  and and_2 (and_2_out, A15, B15, not_4_out, not_1_out);
  and and_3 (and_3_out, not_2_out, B15, Y15, nA_S);
  and and_4 (and_4_out, A15, not_3_out, not_4_out, nA_S);
  or or_1 (FO, and_1_out, and_2_out, and_3_out, and_4_out);
endmodule

/* Test case:
A15  B15  Y15  ~A/S FO
0    0    0    0    0
0    0    1    0    1
0    1    0    0    0
0    1    1    0    0
1    0    0    0    0
1    0    1    0    0
1    1    0    0    1
1    1    1    0    0
0    0    0    1    0
0    0    1    1    0
0    1    0    1    0
0    1    1    1    1
1    0    0    1    1
1    0    1    1    0
1    1    0    1    0
1    1    1    1    0
*/
