// Digital circuit atk16_mem.dig as structural Verilog
module atk16_mem (
  input  [15:0] ADDR,
  input  [15:0] DBUS,
  input  CLK,
  input  MEM_IE,
  input  MEM_OE,
  output MMIO_IE,
  output MMIO_OE,
  output [12:0] MMIO_S
);

  wire and_3_out, and_4_out, MMIO_IE_t, MMIO_OE_t, RAM_IE, RAM_OE, ROM_OE;
  wire [1:0] atk16_mem_mux_1_x;
  wire [14:0] demultiplexer_1_out_0, demultiplexer_1_out_1;
  wire [15:0] MEM_RAM_d, MEM_ROM_d;

  atk16_mem_mux atk16_mem_mux_1 (
    .C(ADDR[13]), .B(ADDR[14]), .A(ADDR[15]), .X(atk16_mem_mux_1_x[0]), .Y(atk16_mem_mux_1_x[1]));
  Demultiplexer #(.Selector_Bits(2), .Bits(15)) demultiplexer_1 (
    .sel(atk16_mem_mux_1_x), .in(ADDR[14:0]), .out_0(demultiplexer_1_out_0), .out_1(demultiplexer_1_out_1));  // open: out_2, out_3
  Decoder #(.Selector_Bits(2)) decoder_1 (
    .sel(atk16_mem_mux_1_x), .out_0(ROM_OE), .out_1(RAM_OE), .out_2(MMIO_OE_t));  // open: out_3
  Demultiplexer #(.Selector_Bits(2)) demultiplexer_2 (
    .sel(atk16_mem_mux_1_x), .in(MEM_IE), .out_1(RAM_IE), .out_2(MMIO_IE_t));  // open: out_0, out_3
  RAMDualPort #(.AddrBits(15), .Bits(16)) MEM_RAM (
    .A(demultiplexer_1_out_1), .Din(DBUS), .str(RAM_IE), .C(CLK), .ld(1'b1), .D(MEM_RAM_d));
  EEPROM #(.AddrBits(15), .isProgramMemory("true"), .Bits(16)) MEM_ROM (
    .A(demultiplexer_1_out_0), .CS(1'b1), .WE(1'b0), .OE(1'b1), .D(MEM_ROM_d));
  // Probe RAM_OUT on MEM_RAM_d
  and and_1 (MMIO_IE, MMIO_IE_t, MEM_IE);
  and and_2 (MMIO_OE, MMIO_OE_t, MEM_OE);
  // Probe ROM_OUT on MEM_ROM_d
  assign DBUS = and_4_out ? MEM_RAM_d : 16'bz;  // Driver driver_1
  assign DBUS = and_3_out ? MEM_ROM_d : 16'bz;  // Driver driver_2
  and and_3 (and_3_out, ROM_OE, MEM_OE);
  and and_4 (and_4_out, RAM_OE, MEM_OE);

  assign MMIO_S = ADDR[12:0];

  // Notes on the sheet:
  //   ADDR: Address
  //   DBUS: Data bus
  //   CLK: Clock
  //   MMIO_IE: Memory-mapped I/O word input enable
  //   MMIO_OE: Memory-mapped I/O word output enable
  //   MEM_IE: Memory input enable
  //   MEM_OE: Memory output enable
  //   MMIO_S: Memory-mapped I/O word selector
  //   contents of MEM_ROM (hex, n*v repeats v):
  //   4014,2e00,6019,13*8000,e0,1a,1a,1a,8000,e000,e001,e002,e800,f800
  //   ,4855,f000,4017,2000,4200,3008,6015,31d8,1fc8,31e0,1fc8,4600,859
  //   ,8404,818,3110,16c8,61fa,1fc9,29c0,1fc9,27c0,31f0,1fc9,2dc0,1fc8
  //   ,5180,800,4019,2000,4235,2240,4400,4c3f,31f0,1fc8,61e2,2dc0,1fc9
  //   ,6001,f840,4442,2480,4220,3088,1488,4248,3088,1488,4245,3088,1488
  //   ,424c,3088,1488,424c,3088,1488,424f,3088,1488,4220,3088,1488,4223
  //   ,3088,1488,4276,3088,1488,4261,3088,1488,4269,3088,1488,426e,3088
  //   ,1488,4263,3088,1488,426f,3088,1488,426f,3088,1488,4264,3088,1488
  //   ,4269,3088,1488,426a,3088,1488,4275,3088,1488,4274,3088,1488,4275
  //   ,3088,1488,4274,3088,1488,14b5,1488,14b7,4220,3088,1488,42bb,3088
  //   ,1488,42bb,3088,1488,42bb,3088,1488,42bb,3088,1488,4220,3088,1488
  //   ,4242,3088,1488,4259,3088,1488,4220,3088,1488,4240,3088,1488,426b
  //   ,3088,1488,4261,3088,1488,426c,3088,1488,425f,3088,1488,426a,3088
  //   ,1488,4261,3088,1488,426e,3088,1488,4220,3088,1488,42bb,3088,1488
  //   ,42bb,3088,1488,42bb,3088,1488,42bb,3088,1488,14b5,1488,14b7,14b5
  //   ,1488,14b7,4220,3088,1488,423e,3088,1488,4220,3088,1488,4a17,2b40
  //   ,4c01,3170,61ff,31c0,1fc8,31c8,1fc8,31d8,1fc8,4016,2000,2000,4215
  //   ,2240,1600,16e9,16e9,8407,1600,16e9,16d9,8410,3080,1488,6012,14b5
  //   ,1488,14b7,4220,3088,1488,423e,3088,1488,4220,3088,1488,6005,1489
  //   ,4220,3088,1488,1489,1fc9,27c0,1fc9,23c0,1fc9,21c0,e000
endmodule

/* Test case:
CLK ADDR   MEM_IE  MEM_OE   DBUS  DBUS_out

# read ROM
program(0xFF)
C   0x0    0       1        Z      0xFF

# read RAM
memory MEM_RAM(0x0)=0x55;
C   0      0       0        Z      X
C   0x8000 0       1        Z      0x55

# write to RAM
C   0x8000 1       0        0xAA   0xAA
C   0x8000 0       1        Z      0xAA
*/
