// Digital circuit atk16_ppu_sprite_eval.dig as structural Verilog
module atk16_ppu_sprite_eval (
  input  clk,
  input  PCLK,
  input  [9:0] SCY,
  input  [15:0] DBUS,
  input  RST,
  output [8:0] SB_D
);

  wire and_1_out, and_2_out, and_3_out, and_8_out, and_9_out, CLK_READA, CLK_READB, CLK_STAGE, CLK_WRITE,
       NPCLK, or_1_out, or_2_out, or_3_out, or_4_out, or_5_out, or_6_out, or_7_out, or_8_out, or_9_out,
       or_10_out, OVF_EVAL, OVF_RENDER, OVF_SECCLR, OVF_SMN, SB_C, SB_ld, SB_str, SEC_C, SEC_ld, SEC_str,
       SM_C, SM_ld, SM_str, SQ_CLR, SQ_READA, SQ_READB, SQ_TRANS, ST_EVAL, ST_IDLE, ST_RENDER, ST_SECCLR,
       TM_C, TM_ld, TM_str, YMATCH;
  wire [1:0] STAGE;
  wire [2:0] SEC_A, SEC_ADDR_2_out, SEC_ADDR_out, SEC_CLR_ADDR_out, Sequencer_out;
  wire [5:0] SM_A;
  wire [10:0] TM_A;
  wire [15:0] SCAN_BUFFER_d;
  wire [17:8] sub_1_s;
  wire [31:0] SEC_D, SEC_Din, SM_D, TM_D;

  or or_1 (or_1_out, OVF_EVAL, OVF_SMN);
  and and_1 (and_1_out, ST_SECCLR, OVF_SECCLR);
  and and_2 (and_2_out, ST_EVAL, or_1_out);
  and and_3 (and_3_out, ST_RENDER, OVF_RENDER);
  or or_2 (or_2_out, CLK_STAGE, RST);
  or or_3 (or_3_out, and_1_out, and_2_out, and_3_out);
  or or_4 (or_4_out, NPCLK, RST);
  or or_5 (or_5_out, RST, SQ_CLR);
  Counter #(.Bits(2)) u_STAGE (.en(1'b1), .C(or_2_out), .clr(RST), .out(STAGE));  // open: ovf
  Counter #(.Bits(3)) Sequencer (.en(1'b1), .C(or_4_out), .clr(or_5_out), .out(Sequencer_out));  // open: ovf
  and and_4 (CLK_READA, SQ_READA, clk);
  and and_5 (CLK_READB, SQ_READB, clk);
  and and_6 (CLK_WRITE, SQ_CLR, clk);
  Decoder #(.Selector_Bits(2)) decoder_1 (
    .sel(STAGE), .out_0(ST_SECCLR), .out_1(ST_EVAL), .out_2(ST_RENDER), .out_3(ST_IDLE));
  and and_7 (CLK_STAGE, or_3_out, clk, SQ_TRANS);
  Break break_1 (.brk(clk));
  not not_1 (NPCLK, clk);
  Decoder #(.Selector_Bits(3)) decoder_2 (
    .sel(Sequencer_out), .out_0(SQ_TRANS), .out_1(SQ_READA), .out_2(SQ_READB), .out_3(SQ_CLR));  // open: out_4, out_5, out_6, out_7
  Break break_2 (.brk(NPCLK));
  LED led_1 (.in(ST_SECCLR));
  LED led_2 (.in(ST_EVAL));
  LED led_3 (.in(ST_RENDER));
  LED led_4 (.in(ST_IDLE));
  or or_6 (or_6_out, CLK_WRITE, RST);
  and and_8 (and_8_out, SQ_CLR, clk, YMATCH);
  or or_7 (or_7_out, and_8_out, RST);
  and and_9 (and_9_out, SQ_READA, clk);
  or or_8 (or_8_out, and_9_out, RST);
  Counter #(.Bits(4)) SEC_CLR_ADDR (
    .en(ST_SECCLR), .C(or_6_out), .clr(RST), .out({OVF_SECCLR, SEC_CLR_ADDR_out}));  // open: ovf
  or or_9 (or_9_out, CLK_WRITE, RST);
  Counter #(.Bits(4)) SEC_ADDR (.en(ST_EVAL), .C(or_7_out), .clr(RST), .out({OVF_EVAL, SEC_ADDR_out}));  // open: ovf
  Counter #(.Bits(4)) SEC_ADDR_2 (
    .en(ST_RENDER), .C(or_8_out), .clr(RST), .out({OVF_RENDER, SEC_ADDR_2_out}));  // open: ovf
  Counter #(.Bits(7)) SMN (.en(ST_EVAL), .C(or_9_out), .clr(RST), .out({OVF_SMN, SM_A}));  // open: ovf
  // Probe on {OVF_SECCLR, SEC_CLR_ADDR_out}
  // Probe on {OVF_SMN, SM_A}
  Sub #(.Bits(10)) sub_1 (.a(SCY), .b(SM_D[17:8]), .c_i(1'b0), .s(sub_1_s));  // open: c_o
  // Probe on {OVF_EVAL, SEC_ADDR_out}
  // Probe on {OVF_RENDER, SEC_ADDR_2_out}
  assign TM_A = ST_RENDER ? {SEC_D[7:0], SEC_D[10:8]} : 11'bz;  // Driver driver_1
  assign SEC_Din = ST_EVAL ? {SM_D[31:18], sub_1_s, SM_D[7:0]} : 32'bz;  // Driver driver_2
  assign SEC_A = ST_SECCLR ? SEC_CLR_ADDR_out : 3'bz;  // Driver driver_3
  assign SEC_Din = ST_SECCLR ? {32{1'b0}} : 32'bz;  // Driver driver_4
  Comparator #(.Bits(10)) comparator_1 (.a(sub_1_s), .b(10'h8), .lt(YMATCH));  // open: gt, eq
  assign SEC_A = ST_EVAL ? SEC_ADDR_out : 3'bz;  // Driver driver_5
  assign SEC_A = ST_RENDER ? SEC_ADDR_2_out : 3'bz;  // Driver driver_6
  or or_10 (or_10_out, CLK_READB, CLK_WRITE);
  Multiplexer #(.Selector_Bits(2)) multiplexer_1 (
    .sel(STAGE), .in_0(1'b0), .in_1(CLK_READA), .in_2(1'b0), .in_3(1'b0), .out(SM_C));
  Multiplexer #(.Selector_Bits(2)) multiplexer_2 (
    .sel(STAGE), .in_0(CLK_WRITE), .in_1(CLK_WRITE), .in_2(CLK_READA), .in_3(1'b0), .out(SEC_C));
  Multiplexer #(.Selector_Bits(2)) multiplexer_3 (
    .sel(STAGE), .in_0(1'b0), .in_1(1'b0), .in_2(or_10_out), .in_3(1'b0), .out(SB_C));
  Multiplexer #(.Selector_Bits(2)) multiplexer_4 (
    .sel(STAGE), .in_0(1'b0), .in_1(1'b0), .in_2(CLK_READB), .in_3(1'b0), .out(TM_C));
  Multiplexer #(.Selector_Bits(2)) multiplexer_5 (
    .sel(STAGE), .in_0(1'b0), .in_1(1'b0), .in_2(1'b0), .in_3(1'b0), .out(SM_str));
  Multiplexer #(.Selector_Bits(2)) multiplexer_6 (
    .sel(STAGE), .in_0(1'b1), .in_1(1'b1), .in_2(1'b0), .in_3(1'b0), .out(SEC_str));
  Multiplexer #(.Selector_Bits(2)) multiplexer_7 (
    .sel(STAGE), .in_0(1'b0), .in_1(1'b0), .in_2(1'b1), .in_3(1'b0), .out(SB_str));
  Multiplexer #(.Selector_Bits(2)) multiplexer_8 (
    .sel(STAGE), .in_0(1'b0), .in_1(1'b0), .in_2(1'b0), .in_3(1'b0), .out(TM_str));
  Multiplexer #(.Selector_Bits(2)) multiplexer_9 (
    .sel(STAGE), .in_0(1'b1), .in_1(1'b1), .in_2(1'b1), .in_3(1'b1), .out(SM_ld));
  Multiplexer #(.Selector_Bits(2)) multiplexer_10 (
    .sel(STAGE), .in_0(1'b1), .in_1(1'b1), .in_2(1'b1), .in_3(1'b1), .out(SEC_ld));
  Multiplexer #(.Selector_Bits(2)) multiplexer_11 (
    .sel(STAGE), .in_0(1'b1), .in_1(1'b1), .in_2(1'b1), .in_3(1'b1), .out(SB_ld));
  Multiplexer #(.Selector_Bits(2)) multiplexer_12 (
    .sel(STAGE), .in_0(1'b1), .in_1(1'b1), .in_2(1'b1), .in_3(1'b1), .out(TM_ld));
  RAMDualPort #(.AddrBits(6), .Bits(16)) SPRITE_MEM_L (
    .A(SM_A), .Din(DBUS), .str(SM_str), .C(SM_C), .ld(SM_ld), .D(SM_D[15:0]));
  RAMDualPort #(.AddrBits(6), .Bits(16)) SPRITE_MEM_H (
    .A(SM_A), .Din(DBUS), .str(SM_str), .C(SM_C), .ld(SM_ld), .D(SM_D[31:16]));
  // Probe on SM_A
  RAMDualPort #(.AddrBits(3), .Bits(32)) SECONDARY (
    .A(SEC_A), .Din(SEC_Din), .str(SEC_str), .C(SEC_C), .ld(SEC_ld), .D(SEC_D));
  RAMDualPort #(.AddrBits(7), .Bits(16)) SCAN_BUFFER (
    .A({7{1'b0}}), .Din({16{1'b0}}), .str(SB_str), .C(SB_C), .ld(SB_ld), .D(SCAN_BUFFER_d));
  RAMDualPort #(.AddrBits(11), .Bits(32)) TILE_MEM (
    .A(TM_A), .Din({32{1'b0}}), .str(TM_str), .C(TM_C), .ld(TM_ld), .D(TM_D));
  // Probe SEC_D on SEC_D
  // Probe SB_D on SCAN_BUFFER_d
  // Probe TM_D on TM_D
  // Probe on SM_D

  assign SB_D = {9{1'b0}};

  // Other names for the same wires on the sheet: PCLK_t = clk; SQ_WRITE = SQ_CLR

  // Notes on the sheet:
  //   clk: Hz: 20
  //   SB_D: Scanline buffer data
  //   SCY: Scanline Y (0..524)
  //   RST: Reset sprite evaluator
  //   8 bits tile pattern index
  //   10 bits Y position
  //   10 bits X position
  //   1 bit H flip
  //   1 bit V flip
  //   1 bit behind background? (priority)
  //   1 bit palette select
  //   = total 4 bytes per sprite
  //   x 64 sprites
  //   = 128 words
  //   State machine & sequencer:
  //   SQ0 transition current state if conditions match
  //   SQ1 read from memory A
  //   SQ2 read from memory B
  //   SQ3 write to memory
  //   SQ4 counter inc
  //   Sequencer clocked by falling edge (NPCLK)
  //   Everything else clocked by rising edge (PCLK)
  //   Stage 1 Secondary Clear
  //   Stage 2 Evaluate sprites
  //   Stage 3 Render line to scanbuf
  //   Stage 4 Idle
  //   Tile mem addr:
  //   8 bits select tile
  //   3 bits select row in tile
  //   = 11 bits total
endmodule
