// Logisim project CPU16.circ as structural Verilog: 9 circuits, main circuit TestBench
module CPU16 (
  input  CLK,
  output HALT,
  output [15:0] RA_OUT
);

  wire ALU_OE, and_1_out, CLK_t, IR_IE, L9_OE, L12_OE, MAR_IE, MEM_IE, MEM_OE, not_1_out, OP_PARITY,
       or_1_out, PC_CO, PC_IE, PC_OE, R1_IE, R1_OE, R2_IE, R2_OE, RESET, US_RS;
  wire [3:0] alu_1_flags, and_3_out, bit_extender_3_out, decoder_1_out0, FR_q, MICROSEQUENCER_q;
  wire [3:1] OPCODE;
  wire [6:0] regbank_1_pb_out;
  wire [7:0] regbank_1_pb_out_3;
  wire [7:7] regbank_1_pb_out_2;
  wire [11:0] IR_12;
  wire [15:0] alu_1_result, bit_extender_1_out, bit_extender_2_out, controlled_buffer_1_out, PC_OUT,
       regbank_1_pa_out, regbank_1_r1_out, regbank_1_r2_out;

  Register #(.trigger("high"), .width(16)) IR (
    .D(controlled_buffer_1_out), .en(IR_IE), .clk(CLK_t), .Q({OPCODE, OP_PARITY, IR_12}), .clr(RESET));
  Button button_1 (.out(RESET));
  Pull_Resistor pull_resistor_1 (.node(PC_CO));
  // NoConnect on regbank_1_pb_out_3
  TTY #(.trigger("falling")) tty_1 (.data(regbank_1_pb_out), .clk(CLK_t), .we(regbank_1_pb_out_2[7]), .clr(RESET));
  Counter #(.max('h7), .width(3)) MICROSEQUENCER (
    .clr(or_1_out), .load(1'b0), .up(1'b1), .count(1'b1), .clk(not_1_out), .Q(MICROSEQUENCER_q[2:0]));  // open: D, carry
  or or_1 (or_1_out, RESET, and_1_out);
  and and_1 (and_1_out, US_RS, not_1_out);
  not not_1 (not_1_out, CLK_t);
  Counter #(.max('hffff), .trigger("falling"), .width(16)) PC (
    .clr(RESET), .load(PC_IE), .up(1'b1), .count(PC_CO), .clk(CLK_t), .D(controlled_buffer_1_out), .Q(PC_OUT));  // open: carry
  Pull_Resistor pull_resistor_2 (.node(PC_IE));
  Pull_Resistor pull_resistor_3 (.node(HALT));
  assign bit_extender_1_out = {{7{1'b0}}, IR_12[8:0]};  // Bit_Extender bit_extender_1
  assign controlled_buffer_1_out = L9_OE ? bit_extender_1_out : 16'bz;  // Controlled_Buffer controlled_buffer_1
  assign bit_extender_2_out = {{4{1'b0}}, IR_12};  // Bit_Extender bit_extender_2
  assign controlled_buffer_1_out = L12_OE ? bit_extender_2_out : 16'bz;  // Controlled_Buffer controlled_buffer_2
  and and_2 (CLK_t, CLK, ~HALT);  // AND_Gate
  RegBank regbank_1 (
    .CLK(CLK_t), .MAIN_BUS_IN(controlled_buffer_1_out), .RESET(RESET), .R1_IE(R1_IE), .R1_OE(R1_OE),
    .R1_S(IR_12[11:9]), .R2_OE(R2_OE), .R2_IE(R2_IE), .R2_S(IR_12[8:6]), .R3_IE(ALU_OE), .R3_S(IR_12[5:3]),
    .MAIN_BUS_OUT(controlled_buffer_1_out), .R1_OUT(regbank_1_r1_out), .R2_OUT(regbank_1_r2_out),
    .PA_OUT(regbank_1_pa_out), .PB_OUT({regbank_1_pb_out_3, regbank_1_pb_out_2[7], regbank_1_pb_out}),
    .RA_OUT(RA_OUT));
  assign controlled_buffer_1_out = PC_OE ? PC_OUT : 16'bz;  // Controlled_Buffer controlled_buffer_3
  // Probe on regbank_1_pa_out
  // Probe on {regbank_1_pb_out_3, regbank_1_pb_out_2[7], regbank_1_pb_out}
  // Probe on regbank_1_r1_out
  // Probe on regbank_1_r2_out
  assign bit_extender_3_out = {{1{OP_PARITY}}, IR_12[2:0]};  // Bit_Extender bit_extender_3
  // NoConnect on IR_12[11]
  // Probe on controlled_buffer_1_out
  Decoder #(.enable("false"), .select(2)) decoder_1 (
    .out0(decoder_1_out0[0]), .out1(decoder_1_out0[1]), .out2(decoder_1_out0[2]), .out3(decoder_1_out0[3]),
    .sel(IR_12[10:9]));
  Pull_Resistor pull_resistor_4 (.node(controlled_buffer_1_out));
  // Probe on controlled_buffer_1_out
  // Probe on alu_1_flags
  ALU alu_1 (
    .S(bit_extender_3_out), .IN_L(regbank_1_r1_out), .IN_R(regbank_1_r2_out), .RESULT(alu_1_result),
    .FLAGS(alu_1_flags));
  assign and_3_out = FR_q & decoder_1_out0;  // AND_Gate and_3, 4 bits wide
  // Probe on alu_1_result
  assign controlled_buffer_1_out = ALU_OE ? alu_1_result : 16'bz;  // Controlled_Buffer controlled_buffer_4
  or or_2 (MICROSEQUENCER_q[3], and_3_out[0], and_3_out[1], and_3_out[2], and_3_out[3]);
  Register #(.trigger("high"), .width(4)) FR (.D(alu_1_flags), .en(ALU_OE), .clk(CLK_t), .Q(FR_q), .clr(RESET));
  ROM #(.dataWidth(16)) UCODE (
    .addr({OPCODE, OP_PARITY, MICROSEQUENCER_q}),
    .data({US_RS, HALT, ALU_OE, L12_OE, L9_OE, IR_IE, R2_OE, R2_IE, R1_OE, R1_IE, MEM_OE, MEM_IE, MAR_IE, PC_OE, PC_IE, PC_CO}));
  // Probe on FR_q
  MemoryModule memorymodule_1 (
    .BUS_IN(controlled_buffer_1_out), .MAR_IE(MAR_IE), .CLK(CLK_t), .RESET(RESET), .MEM_IE(MEM_IE),
    .MEM_OE(MEM_OE), .BUS_OUT(controlled_buffer_1_out));

  // Other names for the same wires on the sheet: OPCODE[0] = OP_PARITY; IR_D3[2:0] = IR_12[2:0];
  //   IR_L9[8:0] = IR_12[8:0]; IR_A3[2:0] = IR_12[11:9]; IR_C3[2:0] = IR_12[5:3]; IR_B3[2:0] = IR_12[8:6]

  // Notes on the sheet:
  //   MAR_IE enables absolute addressing mode
  //   BUS
  //   contents of UCODE (hex, n*v repeats v):
  //   c 421 2000 8000 4*0 c 421 2000 8000 4*0 c 421 2000 8000 4*0 c 421 2000 8000 4*0 c 421 88 120 8000 0
  //   0 0 c 421 88 120 8000 0 0 0 c 421 88 210 8000 0 0 0 c 421 88 210 8000 0 0 0 c 421 840 8000 4*0 c 421
  //   840 8000 4*0 c 421 82 8000 4*0 c 421 82 8000 4*0 c 421 8000 5*0 c 421 202 8000 4*0 c 421 8000 5*0 c
  //   421 8000 5*0 c 421 8000 5*0 c 421 8000 5*0 c 421 8000 5*0 c 421 8000 5*0 c 421 8000 5*0 c 421 8000
  //   5*0 c 421 8000 5*0 c 421 8000 5*0 c 421 8000 5*0 c 421 8000 5*0 c 421 8000 5*0 c 421 8000 5*0 c 421
  //   4000 5*0 c 421 4000
endmodule

module RegBank (
  input  CLK,
  input  [15:0] MAIN_BUS_IN,
  input  RESET,
  input  R1_IE,
  input  R1_OE,
  input  [2:0] R1_S,
  input  R2_OE,
  input  R2_IE,
  input  [2:0] R2_S,
  input  R3_IE,
  input  [2:0] R3_S,
  output [15:0] MAIN_BUS_OUT,
  output [15:0] R1_OUT,
  output [15:0] R2_OUT,
  output [15:0] PA_OUT,
  output [15:0] PB_OUT,
  output [15:0] RA_OUT
);

  wire decoder_1_out0, decoder_1_out1, decoder_1_out2, decoder_1_out3, decoder_1_out4, decoder_1_out5,
       decoder_1_out6, decoder_2_out0, decoder_2_out1, decoder_2_out2, decoder_2_out3, decoder_2_out4,
       decoder_2_out5, decoder_2_out6, decoder_3_out0, decoder_3_out1, decoder_3_out2, decoder_3_out3,
       decoder_3_out4, decoder_3_out5, decoder_3_out6, decoder_4_out0, decoder_4_out1, decoder_4_out2,
       decoder_4_out3, decoder_4_out4, decoder_5_out0, decoder_5_out1, decoder_5_out2, decoder_5_out3,
       decoder_5_out4, or_1_out, or_2_out, or_3_out, or_4_out, or_5_out, or_6_out, or_7_out, or_8_out,
       or_9_out, or_10_out;
  wire [15:0] RB_OUT, RC_OUT, RD_OUT;

  Decoder #(.select(3)) decoder_1 (
    .out0(decoder_1_out0), .out1(decoder_1_out1), .out2(decoder_1_out2), .out3(decoder_1_out3),
    .out4(decoder_1_out4), .out5(decoder_1_out5), .out6(decoder_1_out6), .sel(R1_S), .en(R1_IE));  // open: out7
  Decoder #(.select(3)) decoder_2 (
    .out0(decoder_2_out0), .out1(decoder_2_out1), .out2(decoder_2_out2), .out3(decoder_2_out3),
    .out4(decoder_2_out4), .out5(decoder_2_out5), .out6(decoder_2_out6), .sel(R2_S), .en(R2_IE));  // open: out7
  Decoder #(.select(3)) decoder_3 (
    .out0(decoder_3_out0), .out1(decoder_3_out1), .out2(decoder_3_out2), .out3(decoder_3_out3),
    .out4(decoder_3_out4), .out5(decoder_3_out5), .out6(decoder_3_out6), .sel(R3_S), .en(R3_IE));  // open: out7
  // NoConnect on decoder_1_out0
  // NoConnect on decoder_2_out0
  // NoConnect on decoder_3_out0
  Register #(.trigger("high"), .width(16)) RA (.D(MAIN_BUS_IN), .en(or_1_out), .clk(CLK), .Q(RA_OUT), .clr(RESET));
  or or_1 (or_1_out, decoder_1_out1, decoder_2_out1, decoder_3_out1);
  Register #(.trigger("high"), .width(16)) RC (.D(MAIN_BUS_IN), .en(or_2_out), .clk(CLK), .Q(RC_OUT), .clr(RESET));
  or or_2 (or_2_out, decoder_1_out3, decoder_2_out3, decoder_3_out3);
  or or_3 (or_3_out, decoder_1_out5, decoder_2_out5, decoder_3_out5);
  Register #(.trigger("high"), .width(16)) RB (.D(MAIN_BUS_IN), .en(or_4_out), .clk(CLK), .Q(RB_OUT), .clr(RESET));
  or or_4 (or_4_out, decoder_1_out2, decoder_2_out2, decoder_3_out2);
  Register #(.trigger("high"), .width(16)) RD (.D(MAIN_BUS_IN), .en(or_5_out), .clk(CLK), .Q(RD_OUT), .clr(RESET));
  or or_5 (or_5_out, decoder_1_out4, decoder_2_out4, decoder_3_out4);
  Register #(.trigger("high"), .width(16)) PA (.D(MAIN_BUS_IN), .en(or_3_out), .clk(CLK), .Q(PA_OUT), .clr(RESET));
  or or_6 (or_6_out, decoder_1_out6, decoder_2_out6, decoder_3_out6);
  assign MAIN_BUS_OUT = or_7_out ? RA_OUT : 16'bz;  // Controlled_Buffer controlled_buffer_1
  assign MAIN_BUS_OUT = or_9_out ? RC_OUT : 16'bz;  // Controlled_Buffer controlled_buffer_2
  Register #(.trigger("high"), .width(16)) PB (.D(MAIN_BUS_IN), .en(or_6_out), .clk(CLK), .Q(PB_OUT), .clr(RESET));
  or or_7 (or_7_out, decoder_4_out1, decoder_5_out1);
  assign MAIN_BUS_OUT = or_8_out ? RB_OUT : 16'bz;  // Controlled_Buffer controlled_buffer_3
  or or_8 (or_8_out, decoder_4_out2, decoder_5_out2);
  or or_9 (or_9_out, decoder_4_out3, decoder_5_out3);
  assign MAIN_BUS_OUT = or_10_out ? RD_OUT : 16'bz;  // Controlled_Buffer controlled_buffer_4
  // Probe on MAIN_BUS_IN
  or or_10 (or_10_out, decoder_4_out4, decoder_5_out4);
  // NoConnect on decoder_4_out0
  Decoder #(.select(3)) decoder_4 (
    .out0(decoder_4_out0), .out1(decoder_4_out1), .out2(decoder_4_out2), .out3(decoder_4_out3),
    .out4(decoder_4_out4), .sel(R1_S), .en(R1_OE));  // open: out5, out6, out7
  // NoConnect on decoder_5_out0
  Decoder #(.select(3)) decoder_5 (
    .out0(decoder_5_out0), .out1(decoder_5_out1), .out2(decoder_5_out2), .out3(decoder_5_out3),
    .out4(decoder_5_out4), .sel(R2_S), .en(R2_OE));  // open: out5, out6, out7
  Multiplexer #(.select(3), .width(16)) multiplexer_1 (
    .in0({16{1'b0}}), .in1(RA_OUT), .in2(RB_OUT), .in3(RC_OUT), .in4(RD_OUT), .out(R1_OUT), .sel(R1_S));  // open: in5, in6, in7
  Multiplexer #(.select(3), .width(16)) multiplexer_2 (
    .in0({16{1'b0}}), .in1(RA_OUT), .in2(RB_OUT), .in3(RC_OUT), .in4(RD_OUT), .out(R2_OUT), .sel(R2_S));  // open: in5, in6, in7

  // Other names for the same wires on the sheet: B_IN[15:0] = MAIN_BUS_IN; B_OUT[15:0] = MAIN_BUS_OUT;
  //   R1_S_RB[2:0] = R1_S; R2_S_RB[2:0] = R2_S; R3_S_RB[2:0] = R3_S; RST_RB = RESET

  // Notes on the sheet:
  //   for testbench purposes
endmodule

module ALU (
  input  [3:0] S,
  input  [15:0] IN_L,
  input  [15:0] IN_R,
  output [15:0] RESULT,
  output [3:0] FLAGS
);

  wire and_1_out, and_2_out, decoder_1_out0, decoder_1_out1, decoder_1_out2, ic_74382_1_cn_4_09724fe9,
       ic_74382_2_cn_4_09724fe9, ic_74382_3_cn_4_09724fe9, not_1_out, or_1_out;
  wire [2:0] demultiplexer_1_out0, demultiplexer_1_out1, ic_74382_4_f0;
  wire [3:0] ic_74382_1_f0, ic_74382_2_f0, ic_74382_3_f0;
  wire [15:0] bitshiftleftlogical_1_result, bitshiftrightarithmetic_1_result, bitshiftrightlogical_1_result,
       controlled_buffer_1_out, demultiplexer_2_out0, demultiplexer_2_out1, demultiplexer_2_out2;

  Demultiplexer #(.width(3)) demultiplexer_1 (
    .out0(demultiplexer_1_out0), .out1(demultiplexer_1_out1), .in(S[2:0]), .sel(S[3]));
  Demultiplexer #(.select(3), .width(16)) demultiplexer_2 (
    .out0(demultiplexer_2_out0), .out1(demultiplexer_2_out1), .out2(demultiplexer_2_out2), .in(IN_L),
    .sel(demultiplexer_1_out1));  // open: out3, out4, out5, out6, out7
  // NoConnect on IN_R[7:4]
  // NoConnect on IN_R[11:8]
  // NoConnect on IN_R[15:12]
  Decoder #(.enable("false"), .select(3)) decoder_1 (
    .out0(decoder_1_out0), .out1(decoder_1_out1), .out2(decoder_1_out2), .sel(demultiplexer_1_out1));  // open: out3, out4, out5, out6, out7
  and and_1 (and_1_out, demultiplexer_1_out0[0], ~demultiplexer_1_out0[1], ~demultiplexer_1_out0[2]);  // AND_Gate
  and and_2 (and_2_out, ~demultiplexer_1_out0[0], demultiplexer_1_out0[1], ~demultiplexer_1_out0[2]);  // AND_Gate
  or or_1 (or_1_out, and_1_out, and_2_out);
  IC_74382 ic_74382_1 (
    .Cn(or_1_out), .B0(IN_R[0]), .A0(IN_L[0]), .B1(IN_R[1]), .A1(IN_L[1]), .B2(IN_R[2]), .A2(IN_L[2]),
    .B3(IN_R[3]), .A3(IN_L[3]), .S0(demultiplexer_1_out0[0]), .S1(demultiplexer_1_out0[1]),
    .S2(demultiplexer_1_out0[2]), .F0(ic_74382_1_f0[0]), .F1(ic_74382_1_f0[1]), .F2(ic_74382_1_f0[2]),
    .F3(ic_74382_1_f0[3]), .Cn_4_09724fe9(ic_74382_1_cn_4_09724fe9));  // open: OVR
  IC_74382 ic_74382_2 (
    .Cn(ic_74382_3_cn_4_09724fe9), .B0(IN_R[8]), .A0(IN_L[8]), .B1(IN_R[9]), .A1(IN_L[9]), .B2(IN_R[10]),
    .A2(IN_L[10]), .B3(IN_R[11]), .A3(IN_L[11]), .S0(demultiplexer_1_out0[0]), .S1(demultiplexer_1_out0[1]),
    .S2(demultiplexer_1_out0[2]), .F0(ic_74382_2_f0[0]), .F1(ic_74382_2_f0[1]), .F2(ic_74382_2_f0[2]),
    .F3(ic_74382_2_f0[3]), .Cn_4_09724fe9(ic_74382_2_cn_4_09724fe9));  // open: OVR
  // Probe on ic_74382_1_f0
  // Probe on ic_74382_2_f0
  BitShiftRightLogical bitshiftrightlogical_1 (
    .DATA(demultiplexer_2_out0), .SHIFT_AMT(IN_R[3:0]), .RESULT(bitshiftrightlogical_1_result));
  BitShiftRightArithmetic bitshiftrightarithmetic_1 (
    .DATA(demultiplexer_2_out1), .SHIFT_AMT(IN_R[3:0]), .RESULT(bitshiftrightarithmetic_1_result));
  BitShiftLeftLogical bitshiftleftlogical_1 (
    .DATA(demultiplexer_2_out2), .SHIFT_AMT(IN_R[3:0]), .RESULT(bitshiftleftlogical_1_result));
  IC_74382 ic_74382_3 (
    .Cn(ic_74382_1_cn_4_09724fe9), .B0(IN_R[4]), .A0(IN_L[4]), .B1(IN_R[5]), .A1(IN_L[5]), .B2(IN_R[6]),
    .A2(IN_L[6]), .B3(IN_R[7]), .A3(IN_L[7]), .S0(demultiplexer_1_out0[0]), .S1(demultiplexer_1_out0[1]),
    .S2(demultiplexer_1_out0[2]), .F0(ic_74382_3_f0[0]), .F1(ic_74382_3_f0[1]), .F2(ic_74382_3_f0[2]),
    .F3(ic_74382_3_f0[3]), .Cn_4_09724fe9(ic_74382_3_cn_4_09724fe9));  // open: OVR
  IC_74382 ic_74382_4 (
    .Cn(ic_74382_2_cn_4_09724fe9), .B0(IN_R[12]), .A0(IN_L[12]), .B1(IN_R[13]), .A1(IN_L[13]), .B2(IN_R[14]),
    .A2(IN_L[14]), .B3(IN_R[15]), .A3(IN_L[15]), .S0(demultiplexer_1_out0[0]), .S1(demultiplexer_1_out0[1]),
    .S2(demultiplexer_1_out0[2]), .F0(ic_74382_4_f0[0]), .F1(ic_74382_4_f0[1]), .F2(ic_74382_4_f0[2]),
    .F3(FLAGS[3]), .OVR(FLAGS[1]), .Cn_4_09724fe9(FLAGS[0]));
  assign controlled_buffer_1_out = decoder_1_out0 ? bitshiftrightlogical_1_result : 16'bz;  // Controlled_Buffer controlled_buffer_1
  assign controlled_buffer_1_out = decoder_1_out1 ? bitshiftrightarithmetic_1_result : 16'bz;  // Controlled_Buffer controlled_buffer_2
  assign controlled_buffer_1_out = decoder_1_out2 ? bitshiftleftlogical_1_result : 16'bz;  // Controlled_Buffer controlled_buffer_3
  // Probe on ic_74382_3_f0
  // Probe on {FLAGS[3], ic_74382_4_f0}
  and ZERO (FLAGS[2], ~ic_74382_1_f0[0], ~ic_74382_1_f0[1], ~ic_74382_1_f0[2], ~ic_74382_1_f0[3], ~ic_74382_3_f0[0], ~ic_74382_3_f0[1], ~ic_74382_3_f0[2], ~ic_74382_3_f0[3], ~ic_74382_2_f0[0], ~ic_74382_2_f0[1], ~ic_74382_2_f0[2], ~ic_74382_2_f0[3], ~ic_74382_4_f0[0], ~ic_74382_4_f0[1], ~ic_74382_4_f0[2], ~FLAGS[3]);  // AND_Gate
  not not_1 (not_1_out, S[3]);
  assign RESULT = not_1_out ? {FLAGS[3], ic_74382_4_f0, ic_74382_2_f0, ic_74382_3_f0, ic_74382_1_f0} : 16'bz;  // Controlled_Buffer controlled_buffer_4
  assign RESULT = S[3] ? controlled_buffer_1_out : 16'bz;  // Controlled_Buffer controlled_buffer_5

  // Other names for the same wires on the sheet: CARRY_FL = FLAGS[0]; OVR_FL = FLAGS[1]; ZERO_FL = FLAGS[2];
  //   SIGN_FL = FLAGS[3]; SHIFT_ALU_OE = S[3]

  // Notes on the sheet:
  //   If S = 0XXX, use 74x382 ALU
  //   If S = 1XXX, do bitshift stuff
  //   Carry needs to be forced to 1 when subtracting
  //   Bit shifts are implemented separately here
endmodule

module BitShiftRightLogical (
  input  [15:0] DATA,
  input  [3:0] SHIFT_AMT,
  output [15:0] RESULT
);

  wire [15:0] multiplexer_1_out, multiplexer_2_out, multiplexer_3_out;

  Multiplexer #(.width(16)) multiplexer_1 (
    .in0(DATA), .in1({{8{1'b0}}, DATA[15:8]}), .out(multiplexer_1_out), .sel(SHIFT_AMT[3]));
  Multiplexer #(.width(16)) multiplexer_2 (
    .in0(multiplexer_1_out), .in1({4'b0000, multiplexer_1_out[15:4]}), .out(multiplexer_2_out),
    .sel(SHIFT_AMT[2]));
  Multiplexer #(.width(16)) multiplexer_3 (
    .in0(multiplexer_2_out), .in1({2'b00, multiplexer_2_out[15:2]}), .out(multiplexer_3_out),
    .sel(SHIFT_AMT[1]));
  Multiplexer #(.width(16)) multiplexer_4 (
    .in0(multiplexer_3_out), .in1({1'b0, multiplexer_3_out[15:1]}), .out(RESULT), .sel(SHIFT_AMT[0]));

  // Notes on the sheet:
  //   d >> 8
  //   d >> 4
  //   d >> 2
  //   d >> 1
endmodule

module BitShiftLeftLogical (
  input  [15:0] DATA,
  input  [3:0] SHIFT_AMT,
  output [15:0] RESULT
);

  wire [15:0] multiplexer_1_out, multiplexer_2_out, multiplexer_3_out;

  Multiplexer #(.width(16)) multiplexer_1 (
    .in0(DATA), .in1({DATA[7:0], {8{1'b0}}}), .out(multiplexer_1_out), .sel(SHIFT_AMT[3]));
  Multiplexer #(.width(16)) multiplexer_2 (
    .in0(multiplexer_1_out), .in1({multiplexer_1_out[11:0], 4'b0000}), .out(multiplexer_2_out),
    .sel(SHIFT_AMT[2]));
  Multiplexer #(.width(16)) multiplexer_3 (
    .in0(multiplexer_2_out), .in1({multiplexer_2_out[13:0], 2'b00}), .out(multiplexer_3_out),
    .sel(SHIFT_AMT[1]));
  Multiplexer #(.width(16)) multiplexer_4 (
    .in0(multiplexer_3_out), .in1({multiplexer_3_out[14:0], 1'b0}), .out(RESULT), .sel(SHIFT_AMT[0]));

  // Notes on the sheet:
  //   d >> 8
  //   d >> 4
  //   d >> 2
  //   d >> 1
endmodule

module BitShiftRightArithmetic (
  input  [15:0] DATA,
  input  [3:0] SHIFT_AMT,
  output [15:0] RESULT
);

  wire [15:0] multiplexer_1_out, multiplexer_2_out, multiplexer_3_out;

  Multiplexer #(.width(16)) multiplexer_1 (
    .in0(DATA), .in1({{9{DATA[15]}}, DATA[14:8]}), .out(multiplexer_1_out), .sel(SHIFT_AMT[3]));
  Multiplexer #(.width(16)) multiplexer_2 (
    .in0(multiplexer_1_out), .in1({{5{multiplexer_1_out[15]}}, multiplexer_1_out[14:4]}),
    .out(multiplexer_2_out), .sel(SHIFT_AMT[2]));
  Multiplexer #(.width(16)) multiplexer_3 (
    .in0(multiplexer_2_out), .in1({{3{multiplexer_2_out[15]}}, multiplexer_2_out[14:2]}),
    .out(multiplexer_3_out), .sel(SHIFT_AMT[1]));
  Multiplexer #(.width(16)) multiplexer_4 (
    .in0(multiplexer_3_out), .in1({{2{multiplexer_3_out[15]}}, multiplexer_3_out[14:1]}), .out(RESULT),
    .sel(SHIFT_AMT[0]));

  // Notes on the sheet:
  //   d >> 8
  //   d >> 4
  //   d >> 2
  //   d >> 1
endmodule

module IC_74382 (
  input  Cn,
  input  B0,
  input  A0,
  input  B1,
  input  A1,
  input  B2,
  input  A2,
  input  B3,
  input  A3,
  input  S0,
  input  S1,
  input  S2,
  output F0,
  output F1,
  output F2,
  output F3,
  output OVR,
  output Cn_4_09724fe9
);

  wire and_1_out, and_2_out, and_3_out, and_4_out, and_5_out, and_6_out, and_7_out, and_8_out, and_9_out,
       and_10_out, and_11_out, and_12_out, and_13_out, and_14_out, and_15_out, and_16_out, and_17_out,
       and_18_out, and_19_out, and_20_out, and_21_out, and_22_out, and_23_out, and_24_out, and_25_out,
       and_26_out, and_27_out, and_28_out, and_29_out, and_30_out, and_31_out, and_32_out, and_33_out,
       and_34_out, and_35_out, and_36_out, and_37_out, and_38_out, and_39_out, and_40_out, and_41_out,
       and_42_out, and_43_out, and_44_out, and_45_out, nand_1_out, nand_2_out, nand_3_out, nand_4_out,
       nand_5_out, nand_7_out, nand_8_out, nor_1_out, nor_2_out, nor_3_out, nor_4_out, nor_5_out, nor_6_out,
       nor_7_out, nor_8_out, nor_9_out, nor_10_out, nor_11_out, nor_12_out, nor_13_out, nor_14_out,
       not_1_out, not_2_out, not_3_out, not_4_out, not_5_out, not_6_out, not_7_out, not_8_out, not_9_out,
       not_10_out, not_11_out, not_12_out, not_13_out, not_14_out;

  and and_1 (and_1_out, not_2_out, not_2_out, not_1_out, nand_4_out, nand_8_out);
  nor nor_1 (nor_1_out, and_1_out, and_2_out, and_3_out);
  and and_2 (and_2_out, nand_5_out, nand_4_out, nand_3_out, not_1_out, A0);
  not not_1 (not_1_out, B0);
  and and_3 (and_3_out, nand_8_out, nand_8_out, nand_3_out, B0, not_2_out);
  and and_4 (and_4_out, not_2_out, not_1_out, nand_5_out, nand_3_out, nor_14_out);
  xor xor_1 (F0, nand_1_out, nor_2_out);
  nand nand_1 (nand_1_out, Cn, nor_12_out);
  nor nor_2 (nor_2_out, and_4_out, and_4_out, and_5_out, and_6_out, and_7_out);
  and and_5 (and_5_out, nand_8_out, nand_8_out, nand_4_out, not_1_out, A0);
  not not_2 (not_2_out, A0);
  and and_6 (and_6_out, nand_8_out, nand_8_out, nand_4_out, B0, not_2_out);
  and and_7 (and_7_out, nand_5_out, nand_5_out, nand_3_out, B0, A0);
  and and_8 (and_8_out, not_4_out, not_4_out, not_3_out, nand_4_out, nand_8_out);
  not not_3 (not_3_out, B1);
  nor nor_3 (nor_3_out, and_8_out, and_10_out, and_9_out);
  and and_9 (and_9_out, nand_8_out, nand_8_out, nand_3_out, B1, not_4_out);
  and and_10 (and_10_out, nand_5_out, nand_4_out, nand_3_out, not_3_out, A1);
  and and_11 (and_11_out, Cn, nor_1_out, nor_12_out);
  and and_12 (and_12_out, not_4_out, not_3_out, nand_5_out, nand_3_out, nor_14_out);
  xor xor_2 (F1, nor_4_out, nor_5_out);
  nor nor_4 (nor_4_out, and_11_out, and_13_out);
  and and_13 (and_13_out, nor_1_out, nor_2_out, nor_12_out);
  nor nor_5 (nor_5_out, and_12_out, and_12_out, and_14_out, and_15_out, and_16_out);
  and and_14 (and_14_out, nand_8_out, nand_8_out, nand_4_out, not_3_out, A1);
  not not_4 (not_4_out, A1);
  and and_15 (and_15_out, nand_8_out, nand_8_out, nand_4_out, B1, not_4_out);
  and and_16 (and_16_out, nand_5_out, nand_5_out, nand_3_out, B1, A1);
  nor nor_6 (nor_6_out, and_17_out, and_18_out, and_20_out);
  and and_17 (and_17_out, not_6_out, not_6_out, not_5_out, nand_4_out, nand_8_out);
  and and_18 (and_18_out, nand_5_out, nand_4_out, nand_3_out, not_5_out, A2);
  not not_5 (not_5_out, B2);
  and and_19 (and_19_out, Cn, Cn, nor_1_out, nor_3_out, nor_12_out);
  and and_20 (and_20_out, nand_8_out, nand_8_out, nand_3_out, B2, not_6_out);
  nor nor_7 (nor_7_out, and_19_out, and_21_out, and_23_out);
  and and_21 (and_21_out, nor_1_out, nor_1_out, nor_3_out, nor_2_out, nor_12_out);
  and and_22 (and_22_out, not_6_out, not_5_out, nand_5_out, nand_3_out, nor_14_out);
  not not_6 (not_6_out, A2);
  xor xor_3 (F2, nor_7_out, nor_8_out);
  and and_23 (and_23_out, nor_3_out, nor_5_out, nor_12_out);
  nor nor_8 (nor_8_out, and_22_out, and_22_out, and_24_out, and_25_out, and_26_out);
  and and_24 (and_24_out, nand_8_out, nand_8_out, nand_4_out, not_5_out, A2);
  and and_25 (and_25_out, nand_8_out, nand_8_out, nand_4_out, B2, not_6_out);
  and and_26 (and_26_out, nand_5_out, nand_5_out, nand_3_out, B2, A2);
  and and_27 (and_27_out, not_8_out, not_8_out, not_7_out, nand_4_out, nand_8_out);
  and and_28 (and_28_out, Cn, nor_1_out, nor_3_out, nor_6_out, nor_12_out);
  and and_29 (and_29_out, nor_1_out, nor_3_out, nor_6_out, nor_2_out, nor_12_out);
  nor nor_9 (nor_9_out, and_27_out, and_30_out, and_32_out);
  and and_30 (and_30_out, nand_5_out, nand_4_out, nand_3_out, not_7_out, A3);
  not not_7 (not_7_out, B3);
  nor nor_10 (nor_10_out, and_28_out, and_28_out, and_29_out, and_31_out, and_33_out);
  and and_31 (and_31_out, nor_3_out, nor_3_out, nor_6_out, nor_5_out, nor_12_out);
  and and_32 (and_32_out, nand_8_out, nand_8_out, nand_3_out, B3, not_8_out);
  and and_33 (and_33_out, nor_6_out, nor_8_out, nor_12_out);
  and and_34 (and_34_out, not_8_out, not_7_out, nand_5_out, nand_3_out, nor_14_out);
  and and_35 (and_35_out, nand_8_out, nand_8_out, nand_4_out, not_7_out, A3);
  not not_8 (not_8_out, A3);
  xor xor_4 (F3, nor_10_out, nor_11_out);
  nor nor_11 (nor_11_out, and_34_out, and_34_out, and_35_out, and_36_out, and_38_out);
  and and_36 (and_36_out, nand_8_out, nand_8_out, nand_4_out, B3, not_8_out);
  nand nand_2 (nand_2_out, nor_1_out, nor_1_out, nor_3_out, nor_6_out, nor_9_out);
  and and_37 (and_37_out, nor_1_out, nor_3_out, nor_6_out, nor_9_out, nor_2_out);
  nor nor_12 (nor_12_out, not_13_out, and_40_out);
  and and_38 (and_38_out, nand_5_out, nand_5_out, nand_3_out, B3, A3);
  nor nor_13 (nor_13_out, and_37_out, and_37_out, and_39_out, and_42_out, and_43_out);
  and and_39 (and_39_out, nor_3_out, nor_3_out, nor_6_out, nor_9_out, nor_5_out);
  and and_40 (and_40_out, not_10_out, not_11_out);
  xor xor_5 (OVR, nor_10_out, and_41_out);
  and and_41 (and_41_out, nor_13_out, nand_7_out);
  and and_42 (and_42_out, nor_6_out, nor_9_out, nor_8_out);
  and and_43 (and_43_out, nor_9_out, nor_11_out);
  and and_44 (and_44_out, not_10_out, not_13_out);
  nand nand_3 (nand_3_out, not_9_out, not_12_out, not_14_out);
  nand nand_4 (nand_4_out, not_10_out, not_12_out);
  nand nand_5 (nand_5_out, not_10_out, not_11_out);
  not not_9 (not_9_out, not_10_out);
  not not_10 (not_10_out, S0);
  nand nand_6 (Cn_4_09724fe9, nor_13_out, nand_7_out);
  nand nand_7 (nand_7_out, Cn, nor_1_out, nor_3_out, nor_6_out, nor_9_out);
  nor nor_14 (nor_14_out, and_44_out, and_45_out);
  and and_45 (and_45_out, not_11_out, not_13_out);
  nand nand_8 (nand_8_out, not_11_out, not_14_out);
  not not_11 (not_11_out, S1);
  not not_12 (not_12_out, not_11_out);
  not not_13 (not_13_out, not_14_out);
  not not_14 (not_14_out, S2);

  // Notes on the sheet:
  //   P                                   G      74381 
endmodule

module TestBench (
  input  [7:0] TICK,
  output HALT,
  output [15:0] MEM_OUT
);

  CPU16 cpu16_1 (.CLK(TICK[0]), .HALT(HALT), .RA_OUT(MEM_OUT));
endmodule

module MemoryModule (
  input  [15:0] BUS_IN,
  input  MAR_IE,
  input  CLK,
  input  RESET,
  input  MEM_IE,
  input  MEM_OE,
  output [15:0] BUS_OUT
);

  wire BANK_S, not_1_out;
  wire [14:0] demultiplexer_1_out0, demultiplexer_1_out1, MAR_q;
  wire [15:0] controlled_buffer_1_out, MEM_RAM_dout, MEM_ROM_data;

  Register #(.trigger("high"), .width(16)) MAR (.D(BUS_IN), .en(MAR_IE), .clk(CLK), .Q({BANK_S, MAR_q}), .clr(RESET));
  Demultiplexer #(.width(15)) demultiplexer_1 (
    .out0(demultiplexer_1_out0), .out1(demultiplexer_1_out1), .in(MAR_q), .sel(BANK_S));
  ROM #(.addrWidth(15), .dataWidth(16)) MEM_ROM (.addr(demultiplexer_1_out0), .data(MEM_ROM_data));
  RAM #(.addrWidth(15), .dataWidth(16), .trigger("high")) MEM_RAM (
    .addr(demultiplexer_1_out1), .we(MEM_IE), .oe(1'b1), .din(BUS_IN), .dout(MEM_RAM_dout));
  assign controlled_buffer_1_out = not_1_out ? MEM_ROM_data : 16'bz;  // Controlled_Buffer controlled_buffer_1
  not not_1 (not_1_out, BANK_S);
  assign controlled_buffer_1_out = BANK_S ? MEM_RAM_dout : 16'bz;  // Controlled_Buffer controlled_buffer_2
  assign BUS_OUT = MEM_OE ? controlled_buffer_1_out : 16'bz;  // Controlled_Buffer controlled_buffer_3

  // Notes on the sheet:
  //   ROM = 0000 - 7FFF
  //   RAM = 8000 - FFFF
  //   contents of MEM_ROM (hex, n*v repeats v):
  //   4203 5200 8000 420a 4414 29b 4802 2900 38c0 cb 441e 4812 29a 6500 4202 f000 4201 f000
endmodule
